// Logisim project DigitalClock.circ as structural Verilog: 45 circuits, main circuit Digital Clock (Main)
module Digital_Clock__Main (
  input  _12_Hour_Clock,
  input  _24_Hour_Clock,
  input  Set_Alarm,
  input  Countdown_Timer,
  input  Turn_On_Off_Alarm
);

  wire AM_PM_Toggle_out, and_1_out, button_1_out, hour_w_alarm_function_1_h1_comparer_output,
       hour_w_alarm_function_1_h2_comparer_output, Hours_out, minutes_1_s1_comparer_output,
       minutes_1_s2_comparer_output, Minutes_2_out, n30_second_counter_1_led_light_for_alarm,
       seconds_1_s1_comparer_output, seconds_1_s2_comparer_output, Snooze_Alarm_Initialiser_out;
  wire [1:1] Reset_out;
  wire [6:0] am_to_pm_led_1_out_5;
  wire [13:0] hour_w_alarm_function_1_out_6, minutes_1_out_7, seconds_1_out_7;

  Button Reset (.out(Reset_out[1]));
  LED Alarm (.in(n30_second_counter_1_led_light_for_alarm));
  _30_second_Counter u_30_second_counter_1 (
    .Alarm_on_off(Turn_On_Off_Alarm), .Input(and_1_out), .Snooze(Snooze_Alarm_Initialiser_out),
    .LED_light_for_Alarm(n30_second_counter_1_led_light_for_alarm));
  Button Snooze_Alarm_Initialiser (.out(Snooze_Alarm_Initialiser_out));
  _7_Segment_Display u_7_segment_display_1 (
    .g(hour_w_alarm_function_1_out_6[7]), .f(hour_w_alarm_function_1_out_6[8]),
    .a(hour_w_alarm_function_1_out_6[9]), .b(hour_w_alarm_function_1_out_6[10]),
    .e(hour_w_alarm_function_1_out_6[11]), .d(hour_w_alarm_function_1_out_6[12]),
    .c(hour_w_alarm_function_1_out_6[13]));  // open: dp
  _7_Segment_Display u_7_segment_display_2 (
    .g(hour_w_alarm_function_1_out_6[0]), .f(hour_w_alarm_function_1_out_6[1]),
    .a(hour_w_alarm_function_1_out_6[2]), .b(hour_w_alarm_function_1_out_6[3]),
    .e(hour_w_alarm_function_1_out_6[4]), .d(hour_w_alarm_function_1_out_6[5]),
    .c(hour_w_alarm_function_1_out_6[6]));  // open: dp
  Hour_w__Alarm_Function hour_w_alarm_function_1 (
    ._24_hr_Clock(_24_Hour_Clock), .RESET(Reset_out[1]), ._12_hr_Clock(_12_Hour_Clock),
    .Hour_Setter(Hours_out), .Set_Alarm(Set_Alarm), .out_6(hour_w_alarm_function_1_out_6[0]),
    .out_7(hour_w_alarm_function_1_out_6[1]), .out_8(hour_w_alarm_function_1_out_6[2]),
    .out_9(hour_w_alarm_function_1_out_6[3]), .out_10(hour_w_alarm_function_1_out_6[4]),
    .out_11(hour_w_alarm_function_1_out_6[5]), .out_12(hour_w_alarm_function_1_out_6[6]),
    .out_13(hour_w_alarm_function_1_out_6[7]), .out_14(hour_w_alarm_function_1_out_6[8]),
    .out_15(hour_w_alarm_function_1_out_6[9]), .out_16(hour_w_alarm_function_1_out_6[10]),
    .out_17(hour_w_alarm_function_1_out_6[11]), .out_18(hour_w_alarm_function_1_out_6[12]),
    .out_19(hour_w_alarm_function_1_out_6[13]),
    .H1_Comparer_Output(hour_w_alarm_function_1_h1_comparer_output),
    .H2_Comparer_Output(hour_w_alarm_function_1_h2_comparer_output));  // open: AM_PM_Toggle
  _7_Segment_Display u_7_segment_display_3 (
    .g(minutes_1_out_7[7]), .f(minutes_1_out_7[8]), .a(minutes_1_out_7[9]), .b(minutes_1_out_7[10]),
    .e(minutes_1_out_7[11]), .d(minutes_1_out_7[12]), .c(minutes_1_out_7[13]));  // open: dp
  _7_Segment_Display u_7_segment_display_4 (
    .g(minutes_1_out_7[0]), .f(minutes_1_out_7[1]), .a(minutes_1_out_7[2]), .b(minutes_1_out_7[3]),
    .e(minutes_1_out_7[4]), .d(minutes_1_out_7[5]), .c(minutes_1_out_7[6]));  // open: dp
  and and_1 (and_1_out, hour_w_alarm_function_1_h2_comparer_output, hour_w_alarm_function_1_h1_comparer_output, minutes_1_s2_comparer_output, minutes_1_s1_comparer_output, seconds_1_s2_comparer_output, seconds_1_s1_comparer_output);
  Minutes minutes_1 (
    ._24_hr_Clock_EN(_24_Hour_Clock), .RESET(Reset_out[1]), ._12_hr_Clock_EN(_12_Hour_Clock),
    .Seconds_Set(Minutes_2_out), .Set_Alarm(Set_Alarm), .Count_Down_Timer(Set_Alarm),
    .out_7(minutes_1_out_7[0]), .out_8(minutes_1_out_7[1]), .out_9(minutes_1_out_7[2]),
    .out_10(minutes_1_out_7[3]), .out_11(minutes_1_out_7[4]), .out_12(minutes_1_out_7[5]),
    .out_13(minutes_1_out_7[6]), .out_14(minutes_1_out_7[7]), .out_15(minutes_1_out_7[8]),
    .out_16(minutes_1_out_7[9]), .out_17(minutes_1_out_7[10]), .out_18(minutes_1_out_7[11]),
    .out_19(minutes_1_out_7[12]), .out_20(minutes_1_out_7[13]),
    .S1_Comparer_Output(minutes_1_s1_comparer_output), .S2_Comparer_Output(minutes_1_s2_comparer_output));
  _7_Segment_Display u_7_segment_display_5 (
    .g(seconds_1_out_7[7]), .f(seconds_1_out_7[8]), .a(seconds_1_out_7[9]), .b(seconds_1_out_7[10]),
    .e(seconds_1_out_7[11]), .d(seconds_1_out_7[12]), .c(seconds_1_out_7[13]));  // open: dp
  _7_Segment_Display u_7_segment_display_6 (
    .g(seconds_1_out_7[0]), .f(seconds_1_out_7[1]), .a(seconds_1_out_7[2]), .b(seconds_1_out_7[3]),
    .e(seconds_1_out_7[4]), .d(seconds_1_out_7[5]), .c(seconds_1_out_7[6]));  // open: dp
  AM_to_PM_LED am_to_pm_led_1 (
    ._24_hr_mode_turn_off(_24_Hour_Clock), .Reset(Reset_out[1]), ._12hr_EN(_12_Hour_Clock),
    .Toggler(AM_PM_Toggle_out), .out_5(am_to_pm_led_1_out_5[0]), .out_6(am_to_pm_led_1_out_5[1]),
    .out_7(am_to_pm_led_1_out_5[2]), .out_8(am_to_pm_led_1_out_5[3]), .out_9(am_to_pm_led_1_out_5[4]),
    .out_10(am_to_pm_led_1_out_5[5]), .out_11(am_to_pm_led_1_out_5[6]));
  Seconds seconds_1 (
    ._24_hr_Clock_EN(_24_Hour_Clock), .RESET(Reset_out[1]), ._12_hr_Clock_EN(_12_Hour_Clock),
    .Seconds_Set(button_1_out), .Set_Alarm(Set_Alarm), .Count_Down_Timer(Countdown_Timer),
    .out_7(seconds_1_out_7[0]), .out_8(seconds_1_out_7[1]), .out_9(seconds_1_out_7[2]),
    .out_10(seconds_1_out_7[3]), .out_11(seconds_1_out_7[4]), .out_12(seconds_1_out_7[5]),
    .out_13(seconds_1_out_7[6]), .out_14(seconds_1_out_7[7]), .out_15(seconds_1_out_7[8]),
    .out_16(seconds_1_out_7[9]), .out_17(seconds_1_out_7[10]), .out_18(seconds_1_out_7[11]),
    .out_19(seconds_1_out_7[12]), .out_20(seconds_1_out_7[13]),
    .S1_Comparer_Output(seconds_1_s1_comparer_output), .S2_Comparer_Output(seconds_1_s2_comparer_output));
  _7_Segment_Display u_7_segment_display_7 (
    .g(am_to_pm_led_1_out_5[0]), .f(am_to_pm_led_1_out_5[1]), .a(am_to_pm_led_1_out_5[2]),
    .b(am_to_pm_led_1_out_5[3]), .e(am_to_pm_led_1_out_5[4]), .d(am_to_pm_led_1_out_5[5]),
    .c(am_to_pm_led_1_out_5[6]));  // open: dp
  Button button_1 (.out(button_1_out));
  Button Minutes_2 (.out(Minutes_2_out));
  Button Hours (.out(Hours_out));
  Button AM_PM_Toggle (.out(AM_PM_Toggle_out));

  // Notes on the sheet:
  //   Hours
  //   HH
  //   Minutes
  //   MM
  //   Seconds
  //   SS
  //   AM/PM
  //   Am/Pm
  //   Seconds
endmodule

module BCD_7_Segment_Display (
  input  A,
  input  B,
  input  C,
  input  D,
  output a_2,
  output b_2,
  output c_2,
  output d_2,
  output e,
  output f,
  output g
);

  a a_1 (.A(A), .B(B), .C(C), .D(D), .a_2(a_2));
  b b_1 (.A(A), .B(B), .C(C), .D(D), .b_2(b_2));
  c c_1 (.A(A), .B(B), .C(C), .D(D), .c_2(c_2));
  d d_1 (.A(A), .B(B), .C(C), .D(D), .d_2(d_2));
  e e_1 (.A(A), .B(B), .C(C), .D(D), .e(e));
  f f_1 (.A(A), .B(B), .C(C), .in_4(D), .f(f));
  g g_1 (.A(A), .B(B), .C(C), .D(D), .g(g));
endmodule

module a (
  input  A,
  input  B,
  input  C,
  input  D,
  output a_2
);

  wire and_1_out, and_2_out, and_3_out, not_1_out, not_2_out, not_3_out;

  not not_1 (not_1_out, B);
  not not_2 (not_2_out, C);
  not not_3 (not_3_out, D);
  and and_1 (and_1_out, B, not_2_out);
  and and_2 (and_2_out, not_1_out, C);
  and and_3 (and_3_out, C, not_3_out);
  or or_1 (a_2, A, and_1_out, and_2_out, and_3_out);
endmodule

module b (
  input  A,
  input  B,
  input  C,
  input  D,
  output b_2
);

  wire and_1_out, and_2_out, and_3_out, and_4_out, not_1_out, not_2_out, not_3_out, not_4_out;

  not not_1 (not_1_out, A);
  not not_2 (not_2_out, B);
  not not_3 (not_3_out, C);
  not not_4 (not_4_out, D);
  and and_1 (and_1_out, not_1_out, B, not_3_out);
  and and_2 (and_2_out, A, not_2_out, not_3_out);
  and and_3 (and_3_out, not_1_out, not_3_out, not_4_out);
  and and_4 (and_4_out, not_1_out, B, not_4_out);
  or or_1 (b_2, and_1_out, and_2_out, and_3_out, and_4_out);
endmodule

module c (
  input  A,
  input  B,
  input  C,
  input  D,
  output c_2
);

  wire and_1_out, and_2_out, and_3_out, and_4_out, not_1_out, not_2_out, not_3_out, not_4_out;

  not not_1 (not_1_out, A);
  not not_2 (not_2_out, B);
  not not_3 (not_3_out, C);
  not not_4 (not_4_out, D);
  and and_1 (and_1_out, not_1_out, C);
  and and_2 (and_2_out, A, not_2_out, not_3_out);
  and and_3 (and_3_out, not_1_out, B, D);
  and and_4 (and_4_out, not_2_out, not_3_out, not_4_out);
  or or_1 (c_2, and_1_out, and_2_out, and_3_out, and_4_out);
endmodule

module d (
  input  A,
  input  B,
  input  C,
  input  D,
  output d_2
);

  wire and_1_out, and_2_out, and_3_out, and_4_out, not_1_out, not_2_out, not_3_out, not_4_out;

  not not_1 (not_1_out, A);
  not not_2 (not_2_out, B);
  not not_3 (not_3_out, C);
  not not_4 (not_4_out, D);
  and and_1 (and_1_out, not_1_out, not_2_out);
  and and_2 (and_2_out, not_2_out, not_3_out);
  and and_3 (and_3_out, not_1_out, not_3_out, not_4_out);
  and and_4 (and_4_out, not_1_out, C, D);
  or or_1 (d_2, and_1_out, and_2_out, and_3_out, and_4_out);
endmodule

module e (
  input  A,
  input  B,
  input  C,
  input  D,
  output e
);

  wire and_1_out, and_2_out, not_1_out, not_2_out, not_3_out, not_4_out;

  not not_1 (not_1_out, A);
  not not_2 (not_2_out, B);
  not not_3 (not_3_out, C);
  not not_4 (not_4_out, D);
  and and_1 (and_1_out, not_1_out, C, not_4_out);
  and and_2 (and_2_out, not_2_out, not_3_out, not_4_out);
  or or_1 (e, and_1_out, and_2_out);
endmodule

module f (
  input  A,
  input  B,
  input  C,
  input  in_4,
  output f
);

  wire and_1_out, and_2_out, and_3_out, and_4_out, and_5_out, not_1_out, not_2_out, not_3_out, not_4_out;

  not not_1 (not_1_out, A);
  not not_2 (not_2_out, B);
  not not_3 (not_3_out, C);
  not not_4 (not_4_out, in_4);
  and and_1 (and_1_out, not_1_out, not_2_out, C);
  and and_2 (and_2_out, A, not_2_out, not_3_out);
  and and_3 (and_3_out, not_2_out, not_3_out, not_4_out);
  and and_4 (and_4_out, not_1_out, C, not_4_out);
  and and_5 (and_5_out, not_1_out, B, not_3_out, in_4);
  or or_1 (f, and_1_out, and_2_out, and_3_out, and_4_out, and_5_out);

  // Notes on the sheet:
  //   D
endmodule

module g (
  input  A,
  input  B,
  input  C,
  input  D,
  output g
);

  wire and_1_out, and_2_out, and_3_out, not_1_out, not_2_out, not_3_out;

  not not_1 (not_1_out, A);
  not not_2 (not_2_out, B);
  not not_3 (not_3_out, C);
  and and_1 (and_1_out, not_1_out, B);
  and and_2 (and_2_out, not_2_out, not_3_out);
  and and_3 (and_3_out, not_1_out, D);
  or or_1 (g, and_1_out, and_2_out, and_3_out);
endmodule

module Seconds (
  input  _24_hr_Clock_EN,
  input  RESET,
  input  _12_hr_Clock_EN,
  input  Seconds_Set,
  input  Set_Alarm,
  input  Count_Down_Timer,
  output out_7,
  output out_8,
  output out_9,
  output out_10,
  output out_11,
  output out_12,
  output out_13,
  output out_14,
  output out_15,
  output out_16,
  output out_17,
  output out_18,
  output out_19,
  output out_20,
  output S1_Comparer_Output,
  output S2_Comparer_Output
);

  wire multiplexer_clock_alarm_circuit_3_out_10, or_1_out;
  wire [2:0] modulo_10_modulo_6_connection_s2_1_a2, multiplexer_clock_alarm_circuit_1_out_11,
       multiplexer_clock_alarm_circuit_3_out_11, s2_alarm_1_a2, s2_countdown_1_a2;
  wire [3:0] Alarm_q3, Clock_Down_q3, Clock_Up_q3, Count_Up_Down_Chooser_S1_out_10,
       multiplexer_clock_alarm_circuit_2_out_10;

  or or_1 (or_1_out, _24_hr_Clock_EN, _12_hr_Clock_EN);
  S1Countdown Clock_Down (
    .EN(or_1_out), .Reset(RESET), .Second_setter(Seconds_Set), .Q3(Clock_Down_q3[0]), .Q2(Clock_Down_q3[1]),
    .Q1(Clock_Down_q3[2]), .Q0(Clock_Down_q3[3]));  // open: Overflow
  S2_Countdown s2_countdown_1 (
    .EN(or_1_out), .Reset(RESET), .Seconds_setter_enable(Seconds_Set), .A2(s2_countdown_1_a2[0]),
    .A1(s2_countdown_1_a2[1]), .A0(s2_countdown_1_a2[2]));  // open: Overflow
  Modulo_10_Counter__S1 Clock_Up (
    .EN(or_1_out), .Reset(RESET), .Second_setter(Seconds_Set), .Q3(Clock_Up_q3[0]), .Q2(Clock_Up_q3[1]),
    .Q1(Clock_Up_q3[2]), .Q0(Clock_Up_q3[3]));  // open: Overflow
  Modulo_10___Modulo_6_Connection__S2 modulo_10_modulo_6_connection_s2_1 (
    .EN(or_1_out), .Reset(RESET), .Seconds_setter_enable(Seconds_Set),
    .A2(modulo_10_modulo_6_connection_s2_1_a2[0]), .A1(modulo_10_modulo_6_connection_s2_1_a2[1]),
    .A0(modulo_10_modulo_6_connection_s2_1_a2[2]));  // open: Overflow
  S1_Alarm Alarm (
    .EN(Set_Alarm), .Reset(RESET), .SecondToggle(Seconds_Set), .Q3(Alarm_q3[0]), .Q2(Alarm_q3[1]),
    .Q1(Alarm_q3[2]), .Q0(Alarm_q3[3]));  // open: Overflow
  S2_Alarm s2_alarm_1 (
    .EN(Set_Alarm), .Reset(RESET), .Second_Setter(Seconds_Set), .A2(s2_alarm_1_a2[0]), .A1(s2_alarm_1_a2[1]),
    .A0(s2_alarm_1_a2[2]));
  Multiplexer_Clock__Alarm_circuit Count_Up_Down_Chooser_S1 (
    .in_1(Clock_Up_q3[0]), .Clock(Clock_Up_q3[1]), .in_3(Clock_Up_q3[2]), .in_4(Clock_Up_q3[3]),
    .in_5(Clock_Down_q3[0]), .in_6(Clock_Down_q3[1]), .in_7(Clock_Down_q3[2]), .in_8(Clock_Down_q3[3]),
    .Set_Alarm_CountDownTimer(Count_Down_Timer), .out_10(Count_Up_Down_Chooser_S1_out_10[0]),
    .out_11(Count_Up_Down_Chooser_S1_out_10[1]), .out_12(Count_Up_Down_Chooser_S1_out_10[2]),
    .out_13(Count_Up_Down_Chooser_S1_out_10[3]));
  Multiplexer_Clock__Alarm_circuit multiplexer_clock_alarm_circuit_1 (
    .in_1(1'b0), .Clock(modulo_10_modulo_6_connection_s2_1_a2[0]),
    .in_3(modulo_10_modulo_6_connection_s2_1_a2[1]), .in_4(modulo_10_modulo_6_connection_s2_1_a2[2]),
    .in_5(1'b0), .in_6(s2_countdown_1_a2[0]), .in_7(s2_countdown_1_a2[1]), .in_8(s2_countdown_1_a2[2]),
    .Set_Alarm_CountDownTimer(Count_Down_Timer), .out_11(multiplexer_clock_alarm_circuit_1_out_11[0]),
    .out_12(multiplexer_clock_alarm_circuit_1_out_11[1]), .out_13(multiplexer_clock_alarm_circuit_1_out_11[2]));  // open: out_10
  Multiplexer_Clock__Alarm_circuit multiplexer_clock_alarm_circuit_2 (
    .in_1(Count_Up_Down_Chooser_S1_out_10[0]), .Clock(Count_Up_Down_Chooser_S1_out_10[1]),
    .in_3(Count_Up_Down_Chooser_S1_out_10[2]), .in_4(Count_Up_Down_Chooser_S1_out_10[3]), .in_5(Alarm_q3[0]),
    .in_6(Alarm_q3[1]), .in_7(Alarm_q3[2]), .in_8(Alarm_q3[3]), .Set_Alarm_CountDownTimer(Set_Alarm),
    .out_10(multiplexer_clock_alarm_circuit_2_out_10[0]),
    .out_11(multiplexer_clock_alarm_circuit_2_out_10[1]),
    .out_12(multiplexer_clock_alarm_circuit_2_out_10[2]), .out_13(multiplexer_clock_alarm_circuit_2_out_10[3]));
  Multiplexer_Compare multiplexer_compare_1 (
    .in_1(Count_Up_Down_Chooser_S1_out_10[0]), .in_2(Count_Up_Down_Chooser_S1_out_10[1]),
    .in_3(Count_Up_Down_Chooser_S1_out_10[2]), .in_4(Count_Up_Down_Chooser_S1_out_10[3]), .in_5(Alarm_q3[0]),
    .in_6(Alarm_q3[1]), .in_7(Alarm_q3[2]), .in_8(Alarm_q3[3]), .out_9(S1_Comparer_Output));
  Multiplexer_Clock__Alarm_circuit multiplexer_clock_alarm_circuit_3 (
    .in_1(1'b0), .Clock(multiplexer_clock_alarm_circuit_1_out_11[0]),
    .in_3(multiplexer_clock_alarm_circuit_1_out_11[1]), .in_4(multiplexer_clock_alarm_circuit_1_out_11[2]),
    .in_5(1'b0), .in_6(s2_alarm_1_a2[0]), .in_7(s2_alarm_1_a2[1]), .in_8(s2_alarm_1_a2[2]),
    .Set_Alarm_CountDownTimer(Set_Alarm), .out_10(multiplexer_clock_alarm_circuit_3_out_10),
    .out_11(multiplexer_clock_alarm_circuit_3_out_11[0]),
    .out_12(multiplexer_clock_alarm_circuit_3_out_11[1]), .out_13(multiplexer_clock_alarm_circuit_3_out_11[2]));
  Multiplexer_Compare multiplexer_compare_2 (
    .in_1(1'b0), .in_2(multiplexer_clock_alarm_circuit_1_out_11[0]),
    .in_3(multiplexer_clock_alarm_circuit_1_out_11[1]), .in_4(multiplexer_clock_alarm_circuit_1_out_11[2]),
    .in_5(1'b0), .in_6(s2_alarm_1_a2[0]), .in_7(s2_alarm_1_a2[1]), .in_8(s2_alarm_1_a2[2]),
    .out_9(S2_Comparer_Output));
  BCD_7_Segment_Display bcd_7_segment_display_1 (
    .A(multiplexer_clock_alarm_circuit_2_out_10[0]), .B(multiplexer_clock_alarm_circuit_2_out_10[1]),
    .C(multiplexer_clock_alarm_circuit_2_out_10[2]), .D(multiplexer_clock_alarm_circuit_2_out_10[3]),
    .a_2(out_7), .b_2(out_8), .c_2(out_9), .d_2(out_10), .e(out_11), .f(out_12), .g(out_13));
  BCD_7_Segment_Display bcd_7_segment_display_2 (
    .A(multiplexer_clock_alarm_circuit_3_out_10), .B(multiplexer_clock_alarm_circuit_3_out_11[0]),
    .C(multiplexer_clock_alarm_circuit_3_out_11[1]), .D(multiplexer_clock_alarm_circuit_3_out_11[2]),
    .a_2(out_14), .b_2(out_15), .c_2(out_16), .d_2(out_17), .e(out_18), .f(out_19), .g(out_20));

  // Notes on the sheet:
  //   S2
  //   Alarm Setter
  //   Alarm Setter
  //   S1 Comparer
  //   S2 Comparer
endmodule

module Minutes (
  input  _24_hr_Clock_EN,
  input  RESET,
  input  _12_hr_Clock_EN,
  input  Seconds_Set,
  input  Set_Alarm,
  input  Count_Down_Timer,
  output out_7,
  output out_8,
  output out_9,
  output out_10,
  output out_11,
  output out_12,
  output out_13,
  output out_14,
  output out_15,
  output out_16,
  output out_17,
  output out_18,
  output out_19,
  output out_20,
  output S1_Comparer_Output,
  output S2_Comparer_Output
);

  wire multiplexer_clock_alarm_circuit_3_out_10, or_1_out;
  wire [2:0] m2_alarm_1_a2, m2_countdown_1_a2, m_6_to_m_10_to_m6_for_minutes_m2_1_a2,
       multiplexer_clock_alarm_circuit_1_out_11, multiplexer_clock_alarm_circuit_3_out_11;
  wire [3:0] Alarm_q3, Count_Up_Down_Chooser_S1_out_10, Count_Up_q3, Countdown_q3,
       multiplexer_clock_alarm_circuit_2_out_10;

  or or_1 (or_1_out, _24_hr_Clock_EN, _12_hr_Clock_EN);
  M1_Countdown Countdown (
    .EN(or_1_out), .Reset(RESET), .Minute_setter(Seconds_Set), .Q3(Countdown_q3[0]), .Q2(Countdown_q3[1]),
    .Q1(Countdown_q3[2]), .Q0(Countdown_q3[3]));  // open: Overflow
  M2_Countdown m2_countdown_1 (
    .EN(or_1_out), .Reset(RESET), .Minute_Setter(Seconds_Set), .A2(m2_countdown_1_a2[0]),
    .A1(m2_countdown_1_a2[1]), .A0(m2_countdown_1_a2[2]));  // open: Overflow
  Modulo_6_to_Modulo_10_for_minutes__M1 Count_Up (
    .EN(or_1_out), .Reset(RESET), .Minutes_Setter(Seconds_Set), .Q3(Count_Up_q3[0]), .Q2(Count_Up_q3[1]),
    .Q1(Count_Up_q3[2]), .Q0(Count_Up_q3[3]));  // open: Overflow
  M_6_to_M_10_to_M6_for_minutes__M2 m_6_to_m_10_to_m6_for_minutes_m2_1 (
    .EN(or_1_out), .Reset(RESET), .Minutes_Setter(Seconds_Set),
    .A2(m_6_to_m_10_to_m6_for_minutes_m2_1_a2[0]), .A1(m_6_to_m_10_to_m6_for_minutes_m2_1_a2[1]),
    .A0(m_6_to_m_10_to_m6_for_minutes_m2_1_a2[2]));  // open: Overflow
  M1_Alarm Alarm (
    .EN(Set_Alarm), .Reset(RESET), .Minutes_Setter(Seconds_Set), .Q3(Alarm_q3[0]), .Q2(Alarm_q3[1]),
    .Q1(Alarm_q3[2]), .Q0(Alarm_q3[3]));  // open: Overflow
  M2_Alarm m2_alarm_1 (
    .EN(Set_Alarm), .Reset(RESET), .Minutes_Setter(Seconds_Set), .A2(m2_alarm_1_a2[0]),
    .A1(m2_alarm_1_a2[1]), .A0(m2_alarm_1_a2[2]));
  Multiplexer_Clock__Alarm_circuit Count_Up_Down_Chooser_S1 (
    .in_1(Count_Up_q3[0]), .Clock(Count_Up_q3[1]), .in_3(Count_Up_q3[2]), .in_4(Count_Up_q3[3]),
    .in_5(Countdown_q3[0]), .in_6(Countdown_q3[1]), .in_7(Countdown_q3[2]), .in_8(Countdown_q3[3]),
    .Set_Alarm_CountDownTimer(Count_Down_Timer), .out_10(Count_Up_Down_Chooser_S1_out_10[0]),
    .out_11(Count_Up_Down_Chooser_S1_out_10[1]), .out_12(Count_Up_Down_Chooser_S1_out_10[2]),
    .out_13(Count_Up_Down_Chooser_S1_out_10[3]));
  Multiplexer_Clock__Alarm_circuit multiplexer_clock_alarm_circuit_1 (
    .in_1(1'b0), .Clock(m_6_to_m_10_to_m6_for_minutes_m2_1_a2[0]),
    .in_3(m_6_to_m_10_to_m6_for_minutes_m2_1_a2[1]), .in_4(m_6_to_m_10_to_m6_for_minutes_m2_1_a2[2]),
    .in_5(1'b0), .in_6(m2_countdown_1_a2[0]), .in_7(m2_countdown_1_a2[1]), .in_8(m2_countdown_1_a2[2]),
    .Set_Alarm_CountDownTimer(Count_Down_Timer), .out_11(multiplexer_clock_alarm_circuit_1_out_11[0]),
    .out_12(multiplexer_clock_alarm_circuit_1_out_11[1]), .out_13(multiplexer_clock_alarm_circuit_1_out_11[2]));  // open: out_10
  Multiplexer_Clock__Alarm_circuit multiplexer_clock_alarm_circuit_2 (
    .in_1(Count_Up_Down_Chooser_S1_out_10[0]), .Clock(Count_Up_Down_Chooser_S1_out_10[1]),
    .in_3(Count_Up_Down_Chooser_S1_out_10[2]), .in_4(Count_Up_Down_Chooser_S1_out_10[3]), .in_5(Alarm_q3[0]),
    .in_6(Alarm_q3[1]), .in_7(Alarm_q3[2]), .in_8(Alarm_q3[3]), .Set_Alarm_CountDownTimer(Set_Alarm),
    .out_10(multiplexer_clock_alarm_circuit_2_out_10[0]),
    .out_11(multiplexer_clock_alarm_circuit_2_out_10[1]),
    .out_12(multiplexer_clock_alarm_circuit_2_out_10[2]), .out_13(multiplexer_clock_alarm_circuit_2_out_10[3]));
  Multiplexer_Compare multiplexer_compare_1 (
    .in_1(Count_Up_Down_Chooser_S1_out_10[0]), .in_2(Count_Up_Down_Chooser_S1_out_10[1]),
    .in_3(Count_Up_Down_Chooser_S1_out_10[2]), .in_4(Count_Up_Down_Chooser_S1_out_10[3]), .in_5(Alarm_q3[0]),
    .in_6(Alarm_q3[1]), .in_7(Alarm_q3[2]), .in_8(Alarm_q3[3]), .out_9(S1_Comparer_Output));
  Multiplexer_Clock__Alarm_circuit multiplexer_clock_alarm_circuit_3 (
    .in_1(1'b0), .Clock(multiplexer_clock_alarm_circuit_1_out_11[0]),
    .in_3(multiplexer_clock_alarm_circuit_1_out_11[1]), .in_4(multiplexer_clock_alarm_circuit_1_out_11[2]),
    .in_5(1'b0), .in_6(m2_alarm_1_a2[0]), .in_7(m2_alarm_1_a2[1]), .in_8(m2_alarm_1_a2[2]),
    .Set_Alarm_CountDownTimer(Set_Alarm), .out_10(multiplexer_clock_alarm_circuit_3_out_10),
    .out_11(multiplexer_clock_alarm_circuit_3_out_11[0]),
    .out_12(multiplexer_clock_alarm_circuit_3_out_11[1]), .out_13(multiplexer_clock_alarm_circuit_3_out_11[2]));
  Multiplexer_Compare multiplexer_compare_2 (
    .in_1(1'b0), .in_2(multiplexer_clock_alarm_circuit_1_out_11[0]),
    .in_3(multiplexer_clock_alarm_circuit_1_out_11[1]), .in_4(multiplexer_clock_alarm_circuit_1_out_11[2]),
    .in_5(1'b0), .in_6(m2_alarm_1_a2[0]), .in_7(m2_alarm_1_a2[1]), .in_8(m2_alarm_1_a2[2]),
    .out_9(S2_Comparer_Output));
  BCD_7_Segment_Display bcd_7_segment_display_1 (
    .A(multiplexer_clock_alarm_circuit_2_out_10[0]), .B(multiplexer_clock_alarm_circuit_2_out_10[1]),
    .C(multiplexer_clock_alarm_circuit_2_out_10[2]), .D(multiplexer_clock_alarm_circuit_2_out_10[3]),
    .a_2(out_7), .b_2(out_8), .c_2(out_9), .d_2(out_10), .e(out_11), .f(out_12), .g(out_13));
  BCD_7_Segment_Display bcd_7_segment_display_2 (
    .A(multiplexer_clock_alarm_circuit_3_out_10), .B(multiplexer_clock_alarm_circuit_3_out_11[0]),
    .C(multiplexer_clock_alarm_circuit_3_out_11[1]), .D(multiplexer_clock_alarm_circuit_3_out_11[2]),
    .a_2(out_14), .b_2(out_15), .c_2(out_16), .d_2(out_17), .e(out_18), .f(out_19), .g(out_20));

  // Notes on the sheet:
  //   M2
  //   Alarm Setter
  //   Alarm Setter
  //   M1 Comparer
  //   M2 Comparer
endmodule

module Hour_w__Alarm_Function (
  input  _24_hr_Clock,
  input  RESET,
  input  _12_hr_Clock,
  input  Hour_Setter,
  input  Set_Alarm,
  output out_6,
  output out_7,
  output out_8,
  output out_9,
  output out_10,
  output out_11,
  output out_12,
  output out_13,
  output out_14,
  output out_15,
  output out_16,
  output out_17,
  output out_18,
  output out_19,
  output H1_Comparer_Output,
  output H2_Comparer_Output,
  output AM_PM_Toggle
);

  wire and_2_out, h1_overflow_to_modulo_3_counter_h2_1__12_hr_reset__2,
       h1_overflow_to_modulo_3_counter_h2_1__24_hr_reset__2, m2_overflow_to_m_10_counter_h1_1__12_hr_reset_1,
       m2_overflow_to_m_10_counter_h1_1__24_hr_reset__1, multiplexer_clock_alarm_circuit_2_out_10,
       multiplexer_clock_alarm_circuit_2_out_11, or_1_out, or_2_out;
  wire [1:0] h1_overflow_to_modulo_3_counter_h2_1_b1, h2_alarm_1_b1, multiplexer_clock_alarm_circuit_2_out_12;
  wire [3:0] h1_alarm_1_q3, m2_overflow_to_m_10_counter_h1_1_q3, multiplexer_clock_alarm_circuit_1_out_10;

  or or_1 (or_1_out, _24_hr_Clock, _12_hr_Clock);
  and and_1 (AM_PM_Toggle, _12_hr_Clock, h1_overflow_to_modulo_3_counter_h2_1__12_hr_reset__2, m2_overflow_to_m_10_counter_h1_1__12_hr_reset_1);
  or or_2 (or_2_out, RESET, and_2_out, AM_PM_Toggle);
  M2__overflow_to_M_10_counter_H1 m2_overflow_to_m_10_counter_h1_1 (
    .EN(or_1_out), .Reset(or_2_out), .Hour_Setter(Hour_Setter), .Q3(m2_overflow_to_m_10_counter_h1_1_q3[0]),
    .Q2(m2_overflow_to_m_10_counter_h1_1_q3[1]), .Q1(m2_overflow_to_m_10_counter_h1_1_q3[2]),
    .Q0(m2_overflow_to_m_10_counter_h1_1_q3[3]),
    ._24_hr_Reset__1(m2_overflow_to_m_10_counter_h1_1__24_hr_reset__1),
    ._12_hr_Reset_1(m2_overflow_to_m_10_counter_h1_1__12_hr_reset_1));  // open: Overflow
  H1_overflow_to_Modulo_3_Counter__H2 h1_overflow_to_modulo_3_counter_h2_1 (
    .EN(or_1_out), .RESET(or_2_out), .Hour_Setter(Hour_Setter),
    .B1(h1_overflow_to_modulo_3_counter_h2_1_b1[0]),
    ._24_hr_Reset__2(h1_overflow_to_modulo_3_counter_h2_1__24_hr_reset__2),
    .B0(h1_overflow_to_modulo_3_counter_h2_1_b1[1]),
    ._12_hr_Reset__2(h1_overflow_to_modulo_3_counter_h2_1__12_hr_reset__2));
  H1_Alarm h1_alarm_1 (
    .EN(Set_Alarm), .Reset(or_2_out), .Hour_Setter(Hour_Setter), .Q3(h1_alarm_1_q3[0]),
    .Q2(h1_alarm_1_q3[1]), .Q1(h1_alarm_1_q3[2]), .Q0(h1_alarm_1_q3[3]));  // open: Overflow, _24_hr_Reset__1, _12_hr_Reset_1
  H2_Alarm h2_alarm_1 (
    .EN(Set_Alarm), .RESET(or_2_out), .in_3(Hour_Setter), .B1(h2_alarm_1_b1[0]), .B0(h2_alarm_1_b1[1]));  // open: _24_hr_Reset__2, _12_hr_Reset__2
  and and_2 (and_2_out, h1_overflow_to_modulo_3_counter_h2_1__24_hr_reset__2, m2_overflow_to_m_10_counter_h1_1__24_hr_reset__1);
  Multiplexer_Clock__Alarm_circuit multiplexer_clock_alarm_circuit_1 (
    .in_1(m2_overflow_to_m_10_counter_h1_1_q3[0]), .Clock(m2_overflow_to_m_10_counter_h1_1_q3[1]),
    .in_3(m2_overflow_to_m_10_counter_h1_1_q3[2]), .in_4(m2_overflow_to_m_10_counter_h1_1_q3[3]),
    .in_5(h1_alarm_1_q3[0]), .in_6(h1_alarm_1_q3[1]), .in_7(h1_alarm_1_q3[2]), .in_8(h1_alarm_1_q3[3]),
    .Set_Alarm_CountDownTimer(Set_Alarm), .out_10(multiplexer_clock_alarm_circuit_1_out_10[0]),
    .out_11(multiplexer_clock_alarm_circuit_1_out_10[1]),
    .out_12(multiplexer_clock_alarm_circuit_1_out_10[2]), .out_13(multiplexer_clock_alarm_circuit_1_out_10[3]));
  Multiplexer_Compare multiplexer_compare_1 (
    .in_1(m2_overflow_to_m_10_counter_h1_1_q3[0]), .in_2(m2_overflow_to_m_10_counter_h1_1_q3[1]),
    .in_3(m2_overflow_to_m_10_counter_h1_1_q3[2]), .in_4(m2_overflow_to_m_10_counter_h1_1_q3[3]),
    .in_5(h1_alarm_1_q3[0]), .in_6(h1_alarm_1_q3[1]), .in_7(h1_alarm_1_q3[2]), .in_8(h1_alarm_1_q3[3]),
    .out_9(H1_Comparer_Output));
  Multiplexer_Clock__Alarm_circuit multiplexer_clock_alarm_circuit_2 (
    .in_1(1'b0), .Clock(1'b0), .in_3(h1_overflow_to_modulo_3_counter_h2_1_b1[0]),
    .in_4(h1_overflow_to_modulo_3_counter_h2_1_b1[1]), .in_5(1'b0), .in_6(1'b0), .in_7(h2_alarm_1_b1[0]),
    .in_8(h2_alarm_1_b1[1]), .Set_Alarm_CountDownTimer(Set_Alarm),
    .out_10(multiplexer_clock_alarm_circuit_2_out_10), .out_11(multiplexer_clock_alarm_circuit_2_out_11),
    .out_12(multiplexer_clock_alarm_circuit_2_out_12[0]), .out_13(multiplexer_clock_alarm_circuit_2_out_12[1]));
  Multiplexer_Compare multiplexer_compare_2 (
    .in_1(1'b0), .in_2(1'b0), .in_3(h1_overflow_to_modulo_3_counter_h2_1_b1[0]),
    .in_4(h1_overflow_to_modulo_3_counter_h2_1_b1[1]), .in_5(1'b0), .in_6(1'b0), .in_7(h2_alarm_1_b1[0]),
    .in_8(h2_alarm_1_b1[1]), .out_9(H2_Comparer_Output));
  BCD_7_Segment_Display bcd_7_segment_display_1 (
    .A(multiplexer_clock_alarm_circuit_1_out_10[0]), .B(multiplexer_clock_alarm_circuit_1_out_10[1]),
    .C(multiplexer_clock_alarm_circuit_1_out_10[2]), .D(multiplexer_clock_alarm_circuit_1_out_10[3]),
    .a_2(out_6), .b_2(out_7), .c_2(out_8), .d_2(out_9), .e(out_10), .f(out_11), .g(out_12));
  BCD_7_Segment_Display bcd_7_segment_display_2 (
    .A(multiplexer_clock_alarm_circuit_2_out_10), .B(multiplexer_clock_alarm_circuit_2_out_11),
    .C(multiplexer_clock_alarm_circuit_2_out_12[0]), .D(multiplexer_clock_alarm_circuit_2_out_12[1]),
    .a_2(out_13), .b_2(out_14), .c_2(out_15), .d_2(out_16), .e(out_17), .f(out_18), .g(out_19));

  // Notes on the sheet:
  //   Alarm Setter
  //   Hour Comparer
endmodule

module Hours (
  input  _24_hr_Clock,
  input  RESET,
  input  _12_hr_Clock,
  input  Hour_Setter,
  output out_5,
  output out_6,
  output out_7,
  output out_8,
  output out_9,
  output out_10,
  output out_11,
  output out_12,
  output out_13,
  output out_14,
  output out_15,
  output out_16,
  output out_17,
  output out_18,
  output AM_PM_Toggle
);

  wire and_2_out, h1_overflow_to_modulo_3_counter_h2_1__12_hr_reset__2,
       h1_overflow_to_modulo_3_counter_h2_1__24_hr_reset__2, m2_overflow_to_m_10_counter_h1_1__12_hr_reset_1,
       m2_overflow_to_m_10_counter_h1_1__24_hr_reset__1, or_1_out, or_2_out;
  wire [1:0] h1_overflow_to_modulo_3_counter_h2_1_b1;
  wire [3:0] m2_overflow_to_m_10_counter_h1_1_q3;

  or or_1 (or_1_out, _24_hr_Clock, _12_hr_Clock);
  and and_1 (AM_PM_Toggle, _12_hr_Clock, h1_overflow_to_modulo_3_counter_h2_1__12_hr_reset__2, m2_overflow_to_m_10_counter_h1_1__12_hr_reset_1);
  or or_2 (or_2_out, RESET, and_2_out, AM_PM_Toggle);
  M2__overflow_to_M_10_counter_H1 m2_overflow_to_m_10_counter_h1_1 (
    .EN(or_1_out), .Reset(or_2_out), .Hour_Setter(Hour_Setter), .Q3(m2_overflow_to_m_10_counter_h1_1_q3[0]),
    .Q2(m2_overflow_to_m_10_counter_h1_1_q3[1]), .Q1(m2_overflow_to_m_10_counter_h1_1_q3[2]),
    .Q0(m2_overflow_to_m_10_counter_h1_1_q3[3]),
    ._24_hr_Reset__1(m2_overflow_to_m_10_counter_h1_1__24_hr_reset__1),
    ._12_hr_Reset_1(m2_overflow_to_m_10_counter_h1_1__12_hr_reset_1));  // open: Overflow
  H1_overflow_to_Modulo_3_Counter__H2 h1_overflow_to_modulo_3_counter_h2_1 (
    .EN(or_1_out), .RESET(or_2_out), .Hour_Setter(Hour_Setter),
    .B1(h1_overflow_to_modulo_3_counter_h2_1_b1[0]),
    ._24_hr_Reset__2(h1_overflow_to_modulo_3_counter_h2_1__24_hr_reset__2),
    .B0(h1_overflow_to_modulo_3_counter_h2_1_b1[1]),
    ._12_hr_Reset__2(h1_overflow_to_modulo_3_counter_h2_1__12_hr_reset__2));
  and and_2 (and_2_out, h1_overflow_to_modulo_3_counter_h2_1__24_hr_reset__2, m2_overflow_to_m_10_counter_h1_1__24_hr_reset__1);
  BCD_7_Segment_Display bcd_7_segment_display_1 (
    .A(m2_overflow_to_m_10_counter_h1_1_q3[0]), .B(m2_overflow_to_m_10_counter_h1_1_q3[1]),
    .C(m2_overflow_to_m_10_counter_h1_1_q3[2]), .D(m2_overflow_to_m_10_counter_h1_1_q3[3]), .a_2(out_5),
    .b_2(out_6), .c_2(out_7), .d_2(out_8), .e(out_9), .f(out_10), .g(out_11));
  BCD_7_Segment_Display bcd_7_segment_display_2 (
    .A(1'b0), .B(1'b0), .C(h1_overflow_to_modulo_3_counter_h2_1_b1[0]),
    .D(h1_overflow_to_modulo_3_counter_h2_1_b1[1]), .a_2(out_12), .b_2(out_13), .c_2(out_14), .d_2(out_15),
    .e(out_16), .f(out_17), .g(out_18));
endmodule

module AM_to_PM_LED (
  input  _24_hr_mode_turn_off,
  input  Reset,
  input  _12hr_EN,
  input  Toggler,
  output out_5,
  output out_6,
  output out_7,
  output out_8,
  output out_9,
  output out_10,
  output out_11
);

  wire am_pm_counter_1_c0;

  AM_PM_Counter am_pm_counter_1 (.RESET(Reset), ._12_hr_Clock_EN(_12hr_EN), .Toggler(Toggler), .C0(am_pm_counter_1_c0));
  AM_PM_Display am_pm_display_1 (
    ._24_hr_Mode_TurnOFF(_24_hr_mode_turn_off), .D(am_pm_counter_1_c0), .a(out_5), .b(out_6), .c(out_7),
    .d_2(out_8), .e(out_9), .f(out_10), .g(out_11));
endmodule

module Modulo_10_Counter__S1 (
  input  EN,
  input  Reset,
  input  Second_setter,
  output Q3,
  output Q2,
  output Overflow,
  output Q1,
  output Q0
);

  wire and_1_out, and_2_out, and_3_out, and_4_out, clock_1_out, j_k_ff_1_qn, or_1_out;

  and and_1 (and_1_out, Q2, Q1, Q0);
  and and_2 (and_2_out, Q1, Q0);
  and and_3 (and_3_out, Q1, Q0);
  and and_4 (and_4_out, j_k_ff_1_qn, Q0);
  or or_1 (or_1_out, clock_1_out, Second_setter);
  Clock clock_1 (.out(clock_1_out));
  J_K_Flip_Flop j_k_ff_1 (
    .J(and_1_out), .clk(or_1_out), .K(Q0), .Q(Q3), .Qn(j_k_ff_1_qn), .en(EN), .reset(Reset));  // open: preset
  J_K_Flip_Flop j_k_ff_2 (
    .J(and_2_out), .clk(or_1_out), .K(and_3_out), .Q(Q2), .en(EN), .reset(Reset));  // open: Qn, preset
  J_K_Flip_Flop j_k_ff_3 (.J(and_4_out), .clk(or_1_out), .K(Q0), .Q(Q1), .en(EN), .reset(Reset));  // open: Qn, preset
  J_K_Flip_Flop j_k_ff_4 (.J(1'b1), .clk(or_1_out), .K(1'b1), .Q(Q0), .en(EN), .reset(Reset));  // open: Qn, preset
  nor nor_1 (Overflow, Q3, Q2, Q1, Q0);

  // Notes on the sheet:
  //   Clock
  //   Q3
  //   Q2
  //   Q1
  //   Q0
endmodule

module Modulo_10___Modulo_6_Connection__S2 (
  input  EN,
  input  Reset,
  input  Seconds_setter_enable,
  output A2,
  output Overflow,
  output A1,
  output A0
);

  wire and_1_out, and_2_out, j_k_ff_1_qn, modulo_10_counter_s1_1_overflow;

  Modulo_10_Counter__S1 modulo_10_counter_s1_1 (
    .EN(EN), .Reset(Reset), .Second_setter(Seconds_setter_enable), .Overflow(modulo_10_counter_s1_1_overflow));  // open: Q3, Q2, Q1, Q0
  and and_1 (and_1_out, A1, A0);
  and and_2 (and_2_out, j_k_ff_1_qn, A0);
  J_K_Flip_Flop j_k_ff_1 (
    .J(and_1_out), .clk(modulo_10_counter_s1_1_overflow), .K(A0), .Q(A2), .Qn(j_k_ff_1_qn), .en(EN),
    .reset(Reset));  // open: preset
  J_K_Flip_Flop j_k_ff_2 (
    .J(and_2_out), .clk(modulo_10_counter_s1_1_overflow), .K(A0), .Q(A1), .en(EN), .reset(Reset));  // open: Qn, preset
  J_K_Flip_Flop j_k_ff_3 (
    .J(1'b1), .clk(modulo_10_counter_s1_1_overflow), .K(1'b1), .Q(A0), .en(EN), .reset(Reset));  // open: Qn, preset
  nor nor_1 (Overflow, A2, A1, A0, Seconds_setter_enable);

  // Notes on the sheet:
  //   A2
  //   A1
  //   A0
endmodule

module Modulo_6_to_Modulo_10_for_minutes__M1 (
  input  EN,
  input  Reset,
  input  Minutes_Setter,
  output Q3,
  output Q2,
  output Overflow,
  output Q1,
  output Q0
);

  wire and_1_out, and_2_out, and_3_out, and_4_out, j_k_ff_1_qn, modulo_10_modulo_6_connection_s2_1_overflow,
       or_1_out;

  Modulo_10___Modulo_6_Connection__S2 modulo_10_modulo_6_connection_s2_1 (
    .EN(EN), .Reset(Reset), .Seconds_setter_enable(Minutes_Setter),
    .Overflow(modulo_10_modulo_6_connection_s2_1_overflow));  // open: A2, A1, A0
  or or_1 (or_1_out, modulo_10_modulo_6_connection_s2_1_overflow, Minutes_Setter);
  and and_1 (and_1_out, Q2, Q1, Q0);
  and and_2 (and_2_out, Q1, Q0);
  and and_3 (and_3_out, Q1, Q0);
  and and_4 (and_4_out, j_k_ff_1_qn, Q0);
  J_K_Flip_Flop j_k_ff_1 (
    .J(and_1_out), .clk(or_1_out), .K(Q0), .Q(Q3), .Qn(j_k_ff_1_qn), .en(EN), .reset(Reset));  // open: preset
  J_K_Flip_Flop j_k_ff_2 (
    .J(and_2_out), .clk(or_1_out), .K(and_3_out), .Q(Q2), .en(EN), .reset(Reset));  // open: Qn, preset
  J_K_Flip_Flop j_k_ff_3 (.J(and_4_out), .clk(or_1_out), .K(Q0), .Q(Q1), .en(EN), .reset(Reset));  // open: Qn, preset
  J_K_Flip_Flop j_k_ff_4 (.J(1'b1), .clk(or_1_out), .K(1'b1), .Q(Q0), .en(EN), .reset(Reset));  // open: Qn, preset
  nor nor_1 (Overflow, Q3, Q2, Q1, Q0);

  // Notes on the sheet:
  //   Q3
  //   Q2
  //   Q1
  //   Q0
endmodule

module M_6_to_M_10_to_M6_for_minutes__M2 (
  input  EN,
  input  Reset,
  input  Minutes_Setter,
  output A2,
  output Overflow,
  output A1,
  output A0
);

  wire and_1_out, and_2_out, j_k_ff_1_qn, modulo_6_to_modulo_10_for_minutes_m1_1_overflow;

  Modulo_6_to_Modulo_10_for_minutes__M1 modulo_6_to_modulo_10_for_minutes_m1_1 (
    .EN(EN), .Reset(Reset), .Minutes_Setter(Minutes_Setter),
    .Overflow(modulo_6_to_modulo_10_for_minutes_m1_1_overflow));  // open: Q3, Q2, Q1, Q0
  and and_1 (and_1_out, A1, A0);
  and and_2 (and_2_out, j_k_ff_1_qn, A0);
  J_K_Flip_Flop j_k_ff_1 (
    .J(and_1_out), .clk(modulo_6_to_modulo_10_for_minutes_m1_1_overflow), .K(A0), .Q(A2), .Qn(j_k_ff_1_qn),
    .en(EN), .reset(Reset));  // open: preset
  J_K_Flip_Flop j_k_ff_2 (
    .J(and_2_out), .clk(modulo_6_to_modulo_10_for_minutes_m1_1_overflow), .K(A0), .Q(A1), .en(EN),
    .reset(Reset));  // open: Qn, preset
  J_K_Flip_Flop j_k_ff_3 (
    .J(1'b1), .clk(modulo_6_to_modulo_10_for_minutes_m1_1_overflow), .K(1'b1), .Q(A0), .en(EN), .reset(Reset));  // open: Qn, preset
  nor nor_1 (Overflow, A2, A1, A0, Minutes_Setter);

  // Notes on the sheet:
  //   A2
  //   A1
  //   A0
endmodule

module M2__overflow_to_M_10_counter_H1 (
  input  EN,
  input  Reset,
  input  Hour_Setter,
  output Q3,
  output Q2,
  output Overflow,
  output Q1,
  output Q0,
  output _24_hr_Reset__1,
  output _12_hr_Reset_1
);

  wire and_1_out, and_2_out, and_3_out, and_4_out, j_k_ff_1_qn, j_k_ff_2_qn, j_k_ff_3_qn, j_k_ff_4_qn,
       m_6_to_m_10_to_m6_for_minutes_m2_1_overflow, or_1_out;

  M_6_to_M_10_to_M6_for_minutes__M2 m_6_to_m_10_to_m6_for_minutes_m2_1 (
    .EN(EN), .Reset(Reset), .Minutes_Setter(Hour_Setter),
    .Overflow(m_6_to_m_10_to_m6_for_minutes_m2_1_overflow));  // open: A2, A1, A0
  and and_1 (and_1_out, Q2, Q1, Q0);
  or or_1 (or_1_out, m_6_to_m_10_to_m6_for_minutes_m2_1_overflow, Hour_Setter);
  and and_2 (and_2_out, Q1, Q0);
  and and_3 (and_3_out, Q1, Q0);
  and and_4 (and_4_out, j_k_ff_1_qn, Q0);
  J_K_Flip_Flop j_k_ff_1 (
    .J(and_1_out), .clk(or_1_out), .K(Q0), .Q(Q3), .Qn(j_k_ff_1_qn), .en(EN), .reset(Reset));  // open: preset
  J_K_Flip_Flop j_k_ff_2 (
    .J(and_2_out), .clk(or_1_out), .K(and_3_out), .Q(Q2), .Qn(j_k_ff_2_qn), .en(EN), .reset(Reset));  // open: preset
  J_K_Flip_Flop j_k_ff_3 (
    .J(and_4_out), .clk(or_1_out), .K(Q0), .Q(Q1), .Qn(j_k_ff_3_qn), .en(EN), .reset(Reset));  // open: preset
  J_K_Flip_Flop j_k_ff_4 (
    .J(1'b1), .clk(or_1_out), .K(1'b1), .Q(Q0), .Qn(j_k_ff_4_qn), .en(EN), .reset(Reset));  // open: preset
  nor nor_1 (Overflow, Q3, Q2, Q1, Q0);
  and and_5 (_24_hr_Reset__1, j_k_ff_1_qn, Q2, j_k_ff_3_qn, j_k_ff_4_qn);
  and and_6 (_12_hr_Reset_1, j_k_ff_1_qn, j_k_ff_2_qn, Q1, j_k_ff_4_qn);

  // Notes on the sheet:
  //   Q3
  //   Q2
  //   Q1
  //   Q0
endmodule

module H1_overflow_to_Modulo_3_Counter__H2 (
  input  EN,
  input  RESET,
  input  Hour_Setter,
  output B1,
  output _24_hr_Reset__2,
  output B0,
  output _12_hr_Reset__2
);

  wire j_k_ff_1_qn, m2_overflow_to_m_10_counter_h1_1_overflow;

  M2__overflow_to_M_10_counter_H1 m2_overflow_to_m_10_counter_h1_1 (
    .EN(EN), .Reset(RESET), .Hour_Setter(Hour_Setter), .Overflow(m2_overflow_to_m_10_counter_h1_1_overflow));  // open: Q3, Q2, Q1, Q0, _24_hr_Reset__1, _12_hr_Reset_1
  J_K_Flip_Flop j_k_ff_1 (
    .J(_12_hr_Reset__2), .clk(m2_overflow_to_m_10_counter_h1_1_overflow), .K(1'b1), .Q(_24_hr_Reset__2),
    .Qn(j_k_ff_1_qn), .en(EN), .reset(RESET));  // open: preset
  J_K_Flip_Flop j_k_ff_2 (
    .J(j_k_ff_1_qn), .clk(m2_overflow_to_m_10_counter_h1_1_overflow), .K(1'b1), .Q(_12_hr_Reset__2), .en(EN),
    .reset(RESET));  // open: Qn, preset

  assign B0 = _12_hr_Reset__2;
  assign B1 = _24_hr_Reset__2;

  // Notes on the sheet:
  //   B1
  //   B0
endmodule

module Modulo_6_Counter (
  input  Clock,
  input  Reset,
  output A2,
  output Overflow,
  output A1,
  output A0
);

  wire and_1_out, and_2_out, clock_1_out, j_k_ff_1_qn;

  and and_1 (and_1_out, A1, A0);
  and and_2 (and_2_out, j_k_ff_1_qn, A0);
  Clock clock_1 (.out(clock_1_out));
  J_K_Flip_Flop j_k_ff_1 (
    .J(and_1_out), .clk(clock_1_out), .K(A0), .Q(A2), .Qn(j_k_ff_1_qn), .en(Clock), .reset(Reset));  // open: preset
  J_K_Flip_Flop j_k_ff_2 (
    .J(and_2_out), .clk(clock_1_out), .K(A0), .Q(A1), .en(Clock), .reset(Reset));  // open: Qn, preset
  J_K_Flip_Flop j_k_ff_3 (
    .J(1'b1), .clk(clock_1_out), .K(1'b1), .Q(A0), .en(Clock), .reset(Reset));  // open: Qn, preset
  nor nor_1 (Overflow, A2, A1, A0);

  // Notes on the sheet:
  //   EN
  //   A2
  //   A1
  //   A0
endmodule

module Modulo_3_Counter (
  input  EN,
  input  RESET,
  output B1,
  output B0
);

  wire clock_1_out, j_k_ff_1_qn;

  Clock clock_1 (.out(clock_1_out));
  J_K_Flip_Flop j_k_ff_1 (
    .J(B0), .clk(clock_1_out), .K(1'b1), .Q(B1), .Qn(j_k_ff_1_qn), .en(EN), .reset(RESET));  // open: preset
  J_K_Flip_Flop j_k_ff_2 (
    .J(j_k_ff_1_qn), .clk(clock_1_out), .K(1'b1), .Q(B0), .en(EN), .reset(RESET));  // open: Qn, preset

  // Notes on the sheet:
  //   B1
  //   B0
endmodule

module test_c (
  input  EN,
  input  RESET,
  input  in_3,
  input  in_4,
  input  in_5,
  input  in_6,
  input  RESET_2,
  input  EN_2
);

  wire [2:0] bcd_7_segment_display_1_e, bcd_7_segment_display_2_e, modulo_10_modulo_6_connection_s2_1_a2;
  wire [3:0] bcd_7_segment_display_1_a_2, bcd_7_segment_display_2_a_2, modulo_10_counter_s1_1_q3;
  wire [13:0] hours_1_out_5, minutes_1_out_7, seconds_1_out_7;

  Modulo_10_Counter__S1 modulo_10_counter_s1_1 (
    .EN(EN), .Reset(RESET), .Q3(modulo_10_counter_s1_1_q3[0]), .Q2(modulo_10_counter_s1_1_q3[1]),
    .Q1(modulo_10_counter_s1_1_q3[2]), .Q0(modulo_10_counter_s1_1_q3[3]));  // open: Second_setter, Overflow
  Modulo_10___Modulo_6_Connection__S2 modulo_10_modulo_6_connection_s2_1 (
    .Reset(EN), .Seconds_setter_enable(RESET), .A2(modulo_10_modulo_6_connection_s2_1_a2[0]),
    .A1(modulo_10_modulo_6_connection_s2_1_a2[1]), .A0(modulo_10_modulo_6_connection_s2_1_a2[2]));  // open: EN, Overflow
  _7_Segment_Display u_7_segment_display_1 (
    .g(hours_1_out_5[7]), .f(hours_1_out_5[8]), .a(hours_1_out_5[9]), .b(hours_1_out_5[10]),
    .e(hours_1_out_5[11]), .d(hours_1_out_5[12]), .c(hours_1_out_5[13]));  // open: dp
  Hours hours_1 (
    .RESET(in_4), ._12_hr_Clock(in_3), .out_5(hours_1_out_5[0]), .out_6(hours_1_out_5[1]),
    .out_7(hours_1_out_5[2]), .out_8(hours_1_out_5[3]), .out_9(hours_1_out_5[4]), .out_10(hours_1_out_5[5]),
    .out_11(hours_1_out_5[6]), .out_12(hours_1_out_5[7]), .out_13(hours_1_out_5[8]),
    .out_14(hours_1_out_5[9]), .out_15(hours_1_out_5[10]), .out_16(hours_1_out_5[11]),
    .out_17(hours_1_out_5[12]), .out_18(hours_1_out_5[13]));  // open: _24_hr_Clock, Hour_Setter, AM_PM_Toggle
  _7_Segment_Display u_7_segment_display_2 (
    .g(hours_1_out_5[0]), .f(hours_1_out_5[1]), .a(hours_1_out_5[2]), .b(hours_1_out_5[3]),
    .e(hours_1_out_5[4]), .d(hours_1_out_5[5]), .c(hours_1_out_5[6]));  // open: dp
  _7_Segment_Display u_7_segment_display_3 (
    .g(minutes_1_out_7[7]), .f(minutes_1_out_7[8]), .a(minutes_1_out_7[9]), .b(minutes_1_out_7[10]),
    .e(minutes_1_out_7[11]), .d(minutes_1_out_7[12]), .c(minutes_1_out_7[13]));  // open: dp
  _7_Segment_Display u_7_segment_display_4 (
    .g(minutes_1_out_7[0]), .f(minutes_1_out_7[1]), .a(minutes_1_out_7[2]), .b(minutes_1_out_7[3]),
    .e(minutes_1_out_7[4]), .d(minutes_1_out_7[5]), .c(minutes_1_out_7[6]));  // open: dp
  BCD_7_Segment_Display bcd_7_segment_display_1 (
    .A(modulo_10_counter_s1_1_q3[0]), .B(modulo_10_counter_s1_1_q3[1]), .C(modulo_10_counter_s1_1_q3[2]),
    .D(modulo_10_counter_s1_1_q3[3]), .a_2(bcd_7_segment_display_1_a_2[0]),
    .b_2(bcd_7_segment_display_1_a_2[1]), .c_2(bcd_7_segment_display_1_a_2[2]),
    .d_2(bcd_7_segment_display_1_a_2[3]), .e(bcd_7_segment_display_1_e[0]), .f(bcd_7_segment_display_1_e[1]),
    .g(bcd_7_segment_display_1_e[2]));
  BCD_7_Segment_Display bcd_7_segment_display_2 (
    .A(1'b0), .B(modulo_10_modulo_6_connection_s2_1_a2[0]), .C(modulo_10_modulo_6_connection_s2_1_a2[1]),
    .D(modulo_10_modulo_6_connection_s2_1_a2[2]), .a_2(bcd_7_segment_display_2_a_2[0]),
    .b_2(bcd_7_segment_display_2_a_2[1]), .c_2(bcd_7_segment_display_2_a_2[2]),
    .d_2(bcd_7_segment_display_2_a_2[3]), .e(bcd_7_segment_display_2_e[0]), .f(bcd_7_segment_display_2_e[1]),
    .g(bcd_7_segment_display_2_e[2]));
  Minutes minutes_1 (
    .RESET(in_6), ._12_hr_Clock_EN(in_5), .out_7(minutes_1_out_7[0]), .out_8(minutes_1_out_7[1]),
    .out_9(minutes_1_out_7[2]), .out_10(minutes_1_out_7[3]), .out_11(minutes_1_out_7[4]),
    .out_12(minutes_1_out_7[5]), .out_13(minutes_1_out_7[6]), .out_14(minutes_1_out_7[7]),
    .out_15(minutes_1_out_7[8]), .out_16(minutes_1_out_7[9]), .out_17(minutes_1_out_7[10]),
    .out_18(minutes_1_out_7[11]), .out_19(minutes_1_out_7[12]), .out_20(minutes_1_out_7[13]),
    .S2_Comparer_Output(hours_1_out_5[0]));  // open: _24_hr_Clock_EN, Seconds_Set, Set_Alarm, Count_Down_Timer, S1_Comparer_Output
  _7_Segment_Display u_7_segment_display_5 (
    .g(seconds_1_out_7[7]), .f(seconds_1_out_7[8]), .a(seconds_1_out_7[9]), .b(seconds_1_out_7[10]),
    .e(seconds_1_out_7[11]), .d(seconds_1_out_7[12]), .c(seconds_1_out_7[13]));  // open: dp
  _7_Segment_Display u_7_segment_display_6 (
    .g(seconds_1_out_7[0]), .f(seconds_1_out_7[1]), .a(seconds_1_out_7[2]), .b(seconds_1_out_7[3]),
    .e(seconds_1_out_7[4]), .d(seconds_1_out_7[5]), .c(seconds_1_out_7[6]));  // open: dp
  Seconds seconds_1 (
    .RESET(EN_2), ._12_hr_Clock_EN(RESET_2), .out_7(seconds_1_out_7[0]), .out_8(seconds_1_out_7[1]),
    .out_9(seconds_1_out_7[2]), .out_10(seconds_1_out_7[3]), .out_11(seconds_1_out_7[4]),
    .out_12(seconds_1_out_7[5]), .out_13(seconds_1_out_7[6]), .out_14(seconds_1_out_7[7]),
    .out_15(seconds_1_out_7[8]), .out_16(seconds_1_out_7[9]), .out_17(seconds_1_out_7[10]),
    .out_18(seconds_1_out_7[11]), .out_19(seconds_1_out_7[12]), .out_20(seconds_1_out_7[13]),
    .S1_Comparer_Output(minutes_1_out_7[0]), .S2_Comparer_Output(minutes_1_out_7[1]));  // open: _24_hr_Clock_EN, Seconds_Set, Set_Alarm, Count_Down_Timer
  _7_Segment_Display u_7_segment_display_7 (
    .g(bcd_7_segment_display_2_a_2[0]), .f(bcd_7_segment_display_2_a_2[1]),
    .a(bcd_7_segment_display_2_a_2[2]), .b(bcd_7_segment_display_2_a_2[3]), .e(bcd_7_segment_display_2_e[0]),
    .d(bcd_7_segment_display_2_e[1]), .c(bcd_7_segment_display_2_e[2]));  // open: dp
  _7_Segment_Display u_7_segment_display_8 (
    .g(bcd_7_segment_display_1_a_2[0]), .f(bcd_7_segment_display_1_a_2[1]),
    .a(bcd_7_segment_display_1_a_2[2]), .b(bcd_7_segment_display_1_a_2[3]), .e(bcd_7_segment_display_1_e[0]),
    .d(bcd_7_segment_display_1_e[1]), .c(bcd_7_segment_display_1_e[2]));  // open: dp

  // Notes on the sheet:
  //   Hours
  //   Minutes
  //   Seconds
endmodule

module _12HourCounter_H1 (
  input  EN,
  input  Reset,
  output Q3,
  output Q2,
  output Overflow,
  output Q1,
  output Q0,
  output _12_hr_Reset__1
);

  wire and_1_out, and_2_out, and_3_out, and_4_out, j_k_ff_1_qn, j_k_ff_2_qn, j_k_ff_4_qn,
       m_6_to_m_10_to_m6_for_minutes_m2_1_overflow;

  M_6_to_M_10_to_M6_for_minutes__M2 m_6_to_m_10_to_m6_for_minutes_m2_1 (
    .Reset(EN), .Minutes_Setter(Reset), .Overflow(m_6_to_m_10_to_m6_for_minutes_m2_1_overflow));  // open: EN, A2, A1, A0
  and and_1 (and_1_out, Q2, Q1, Q0);
  and and_2 (and_2_out, Q1, Q0);
  and and_3 (and_3_out, Q1, Q0);
  and and_4 (and_4_out, j_k_ff_1_qn, Q0);
  J_K_Flip_Flop j_k_ff_1 (
    .J(and_1_out), .clk(m_6_to_m_10_to_m6_for_minutes_m2_1_overflow), .K(Q0), .Q(Q3), .Qn(j_k_ff_1_qn),
    .en(EN), .reset(Reset));  // open: preset
  J_K_Flip_Flop j_k_ff_2 (
    .J(and_2_out), .clk(m_6_to_m_10_to_m6_for_minutes_m2_1_overflow), .K(and_3_out), .Q(Q2),
    .Qn(j_k_ff_2_qn), .en(EN), .reset(Reset));  // open: preset
  J_K_Flip_Flop j_k_ff_3 (
    .J(and_4_out), .clk(m_6_to_m_10_to_m6_for_minutes_m2_1_overflow), .K(Q0), .Q(Q1), .en(EN), .reset(Reset));  // open: Qn, preset
  J_K_Flip_Flop j_k_ff_4 (
    .J(1'b1), .clk(m_6_to_m_10_to_m6_for_minutes_m2_1_overflow), .K(1'b1), .Q(Q0), .Qn(j_k_ff_4_qn), .en(EN),
    .reset(Reset));  // open: preset
  nor nor_1 (Overflow, Q3, Q2, Q1, Q0);
  and and_5 (_12_hr_Reset__1, j_k_ff_1_qn, j_k_ff_2_qn, Q1, j_k_ff_4_qn);

  // Notes on the sheet:
  //   Q3
  //   Q2
  //   Q1
  //   Q0
endmodule

module _12HourCounter_H2 (
  input  EN,
  input  RESET,
  output B1,
  output _12_hr_Reset__2,
  output B0,
  output AM_PM_Overflow
);

  wire j_k_ff_1_qn, n12hourcounter_h1_1_overflow;

  _12HourCounter_H1 u_12hourcounter_h1_1 (
    .EN(EN), .Reset(RESET), .Overflow(n12hourcounter_h1_1_overflow));  // open: Q3, Q2, Q1, Q0, _12_hr_Reset__1
  J_K_Flip_Flop j_k_ff_1 (
    .J(_12_hr_Reset__2), .clk(n12hourcounter_h1_1_overflow), .K(1'b1), .Q(B1), .Qn(j_k_ff_1_qn), .en(EN),
    .reset(RESET));  // open: preset
  J_K_Flip_Flop j_k_ff_2 (
    .J(j_k_ff_1_qn), .clk(n12hourcounter_h1_1_overflow), .K(1'b1), .Q(_12_hr_Reset__2), .en(EN), .reset(RESET));  // open: Qn, preset
  nor nor_1 (AM_PM_Overflow, B1, _12_hr_Reset__2);

  assign B0 = _12_hr_Reset__2;

  // Notes on the sheet:
  //   B1
  //   B0
endmodule

module AM_PM_Counter (
  input  RESET,
  input  _12_hr_Clock_EN,
  input  Toggler,
  output C0
);

  wire hours_1_am_pm_toggle, or_1_out;

  Hours hours_1 (
    ._24_hr_Clock(1'b0), .RESET(RESET), ._12_hr_Clock(_12_hr_Clock_EN), .Hour_Setter(Toggler),
    .AM_PM_Toggle(hours_1_am_pm_toggle));  // open: out_5, out_6, out_7, out_8, out_9, out_10, out_11, out_12, out_13, out_14, out_15, out_16, out_17, out_18
  or or_1 (or_1_out, hours_1_am_pm_toggle, Toggler);
  J_K_Flip_Flop J0_K0 (
    .J(1'b1), .clk(or_1_out), .K(1'b1), .Q(C0), .en(_12_hr_Clock_EN), .reset(RESET));  // open: Qn, preset
endmodule

module AM_PM_Display (
  input  _24_hr_Mode_TurnOFF,
  input  D,
  output a,
  output b,
  output c,
  output d_2,
  output e,
  output f,
  output g
);

  wire not_1_out, not_2_out;

  not not_1 (not_1_out, _24_hr_Mode_TurnOFF);
  not not_2 (not_2_out, D);
  and and_1 (a, not_1_out, 1'b1);
  and and_2 (g, not_1_out, not_2_out);

  assign b = a;
  assign c = a;
  assign d_2 = a;
  assign e = a;
  assign f = 1'b0;
endmodule

module _24To12_Changer (
  input  _24HrClock,
  input  RESET,
  input  _12HrClock,
  output out_4,
  output out_5,
  output out_6,
  output out_7,
  output out_8,
  output out_9,
  output out_10,
  output out_11,
  output out_12,
  output out_13,
  output out_14,
  output out_15,
  output out_16,
  output out_17
);

  wire and_1_out, and_2_out, h1_overflow_to_modulo_3_counter_h2_1__24_hr_reset__2,
       m2_overflow_to_m_10_counter_h1_1__24_hr_reset__1, n12hourcounter_h1_1__12_hr_reset__1,
       n12hourcounter_h2_1__12_hr_reset__2, or_1_out;
  wire [1:0] h1_overflow_to_modulo_3_counter_h2_1_b1, n12hourcounter_h2_1_b1;
  wire [3:0] m2_overflow_to_m_10_counter_h1_1_q3, n12hourcounter_h1_1_q3;
  wire [6:0] bcd_7_segment_display_1_a_2, bcd_7_segment_display_2_a_2, bcd_7_segment_display_3_a_2,
       bcd_7_segment_display_4_a_2;

  or or_1 (or_1_out, RESET, and_2_out, and_1_out);
  M2__overflow_to_M_10_counter_H1 m2_overflow_to_m_10_counter_h1_1 (
    .EN(_24HrClock), .Reset(or_1_out), .Q3(m2_overflow_to_m_10_counter_h1_1_q3[0]),
    .Q2(m2_overflow_to_m_10_counter_h1_1_q3[1]), .Q1(m2_overflow_to_m_10_counter_h1_1_q3[2]),
    .Q0(m2_overflow_to_m_10_counter_h1_1_q3[3]),
    ._24_hr_Reset__1(m2_overflow_to_m_10_counter_h1_1__24_hr_reset__1));  // open: Hour_Setter, Overflow, _12_hr_Reset_1
  H1_overflow_to_Modulo_3_Counter__H2 h1_overflow_to_modulo_3_counter_h2_1 (
    .EN(_24HrClock), .RESET(or_1_out), .B1(h1_overflow_to_modulo_3_counter_h2_1_b1[0]),
    ._24_hr_Reset__2(h1_overflow_to_modulo_3_counter_h2_1__24_hr_reset__2),
    .B0(h1_overflow_to_modulo_3_counter_h2_1_b1[1]));  // open: Hour_Setter, _12_hr_Reset__2
  and and_1 (and_1_out, h1_overflow_to_modulo_3_counter_h2_1__24_hr_reset__2, m2_overflow_to_m_10_counter_h1_1__24_hr_reset__1);
  _12HourCounter_H1 u_12hourcounter_h1_1 (
    .EN(_12HrClock), .Reset(or_1_out), .Q3(n12hourcounter_h1_1_q3[0]), .Q2(n12hourcounter_h1_1_q3[1]),
    .Q1(n12hourcounter_h1_1_q3[2]), .Q0(n12hourcounter_h1_1_q3[3]),
    ._12_hr_Reset__1(n12hourcounter_h1_1__12_hr_reset__1));  // open: Overflow
  _12HourCounter_H2 u_12hourcounter_h2_1 (
    .EN(_12HrClock), .RESET(or_1_out), .B1(n12hourcounter_h2_1_b1[0]),
    ._12_hr_Reset__2(n12hourcounter_h2_1__12_hr_reset__2), .B0(n12hourcounter_h2_1_b1[1]));  // open: AM_PM_Overflow
  and and_2 (and_2_out, n12hourcounter_h2_1__12_hr_reset__2, n12hourcounter_h1_1__12_hr_reset__1);
  BCD_7_Segment_Display bcd_7_segment_display_1 (
    .A(m2_overflow_to_m_10_counter_h1_1_q3[0]), .B(m2_overflow_to_m_10_counter_h1_1_q3[1]),
    .C(m2_overflow_to_m_10_counter_h1_1_q3[2]), .D(m2_overflow_to_m_10_counter_h1_1_q3[3]),
    .a_2(bcd_7_segment_display_1_a_2[0]), .b_2(bcd_7_segment_display_1_a_2[1]),
    .c_2(bcd_7_segment_display_1_a_2[2]), .d_2(bcd_7_segment_display_1_a_2[3]),
    .e(bcd_7_segment_display_1_a_2[4]), .f(bcd_7_segment_display_1_a_2[5]), .g(bcd_7_segment_display_1_a_2[6]));
  BCD_7_Segment_Display bcd_7_segment_display_2 (
    .A(1'b0), .B(1'b0), .C(h1_overflow_to_modulo_3_counter_h2_1_b1[0]),
    .D(h1_overflow_to_modulo_3_counter_h2_1_b1[1]), .a_2(bcd_7_segment_display_2_a_2[0]),
    .b_2(bcd_7_segment_display_2_a_2[1]), .c_2(bcd_7_segment_display_2_a_2[2]),
    .d_2(bcd_7_segment_display_2_a_2[3]), .e(bcd_7_segment_display_2_a_2[4]),
    .f(bcd_7_segment_display_2_a_2[5]), .g(bcd_7_segment_display_2_a_2[6]));
  BCD_7_Segment_Display bcd_7_segment_display_3 (
    .A(n12hourcounter_h1_1_q3[0]), .B(n12hourcounter_h1_1_q3[1]), .C(n12hourcounter_h1_1_q3[2]),
    .D(n12hourcounter_h1_1_q3[3]), .a_2(bcd_7_segment_display_3_a_2[0]),
    .b_2(bcd_7_segment_display_3_a_2[1]), .c_2(bcd_7_segment_display_3_a_2[2]),
    .d_2(bcd_7_segment_display_3_a_2[3]), .e(bcd_7_segment_display_3_a_2[4]),
    .f(bcd_7_segment_display_3_a_2[5]), .g(bcd_7_segment_display_3_a_2[6]));
  BCD_7_Segment_Display bcd_7_segment_display_4 (
    .A(1'b0), .B(1'b0), .C(n12hourcounter_h2_1_b1[0]), .D(n12hourcounter_h2_1_b1[1]),
    .a_2(bcd_7_segment_display_4_a_2[0]), .b_2(bcd_7_segment_display_4_a_2[1]),
    .c_2(bcd_7_segment_display_4_a_2[2]), .d_2(bcd_7_segment_display_4_a_2[3]),
    .e(bcd_7_segment_display_4_a_2[4]), .f(bcd_7_segment_display_4_a_2[5]), .g(bcd_7_segment_display_4_a_2[6]));
  or or_2 (out_4, bcd_7_segment_display_1_a_2[0], bcd_7_segment_display_3_a_2[0]);
  or or_3 (out_5, bcd_7_segment_display_1_a_2[1], bcd_7_segment_display_3_a_2[1]);
  or or_4 (out_6, bcd_7_segment_display_1_a_2[2], bcd_7_segment_display_3_a_2[2]);
  or or_5 (out_7, bcd_7_segment_display_1_a_2[3], bcd_7_segment_display_3_a_2[3]);
  or or_6 (out_8, bcd_7_segment_display_1_a_2[4], bcd_7_segment_display_3_a_2[4]);
  or or_7 (out_9, bcd_7_segment_display_1_a_2[5], bcd_7_segment_display_3_a_2[5]);
  or or_8 (out_10, bcd_7_segment_display_1_a_2[6], bcd_7_segment_display_3_a_2[6]);
  or or_9 (out_11, bcd_7_segment_display_2_a_2[0], bcd_7_segment_display_4_a_2[0]);
  or or_10 (out_12, bcd_7_segment_display_2_a_2[1], bcd_7_segment_display_4_a_2[1]);
  or or_11 (out_13, bcd_7_segment_display_2_a_2[2], bcd_7_segment_display_4_a_2[2]);
  or or_12 (out_14, bcd_7_segment_display_2_a_2[3], bcd_7_segment_display_4_a_2[3]);
  or or_13 (out_15, bcd_7_segment_display_2_a_2[4], bcd_7_segment_display_4_a_2[4]);
  or or_14 (out_16, bcd_7_segment_display_2_a_2[5], bcd_7_segment_display_4_a_2[5]);
  or or_15 (out_17, bcd_7_segment_display_2_a_2[6], bcd_7_segment_display_4_a_2[6]);
endmodule

module _24hr___12hr_clock_test (
  input  in_1,
  input  RESET,
  input  in_3
);

  wire [6:0] am_to_pm_led_1_out_5;
  wire [13:0] minutes_1_out_7, seconds_1_out_7, test_2_1_out_3;

  _7_Segment_Display u_7_segment_display_1 (
    .g(test_2_1_out_3[7]), .f(test_2_1_out_3[8]), .a(test_2_1_out_3[9]), .b(test_2_1_out_3[10]),
    .e(test_2_1_out_3[11]), .d(test_2_1_out_3[12]), .c(test_2_1_out_3[13]));  // open: dp
  _7_Segment_Display u_7_segment_display_2 (
    .g(test_2_1_out_3[0]), .f(test_2_1_out_3[1]), .a(test_2_1_out_3[2]), .b(test_2_1_out_3[3]),
    .e(test_2_1_out_3[4]), .d(test_2_1_out_3[5]), .c(test_2_1_out_3[6]));  // open: dp
  test_2 test_2_1 (
    .EN(in_1), .RESET(RESET), .out_3(test_2_1_out_3[0]), .out_4(test_2_1_out_3[1]),
    .out_5(test_2_1_out_3[2]), .out_6(test_2_1_out_3[3]), .out_7(test_2_1_out_3[4]),
    .out_8(test_2_1_out_3[5]), .out_9(test_2_1_out_3[6]), .out_10(test_2_1_out_3[7]),
    .out_11(test_2_1_out_3[8]), .out_12(test_2_1_out_3[9]), .out_13(test_2_1_out_3[10]),
    .out_14(test_2_1_out_3[11]), .out_15(test_2_1_out_3[12]), .out_16(test_2_1_out_3[13]));  // open: out_17
  _7_Segment_Display u_7_segment_display_3 (
    .g(minutes_1_out_7[7]), .f(minutes_1_out_7[8]), .a(minutes_1_out_7[9]), .b(minutes_1_out_7[10]),
    .e(minutes_1_out_7[11]), .d(minutes_1_out_7[12]), .c(minutes_1_out_7[13]));  // open: dp
  Minutes minutes_1 (
    .RESET(in_3), ._12_hr_Clock_EN(RESET), .out_7(minutes_1_out_7[0]), .out_8(minutes_1_out_7[1]),
    .out_9(minutes_1_out_7[2]), .out_10(minutes_1_out_7[3]), .out_11(minutes_1_out_7[4]),
    .out_12(minutes_1_out_7[5]), .out_13(minutes_1_out_7[6]), .out_14(minutes_1_out_7[7]),
    .out_15(minutes_1_out_7[8]), .out_16(minutes_1_out_7[9]), .out_17(minutes_1_out_7[10]),
    .out_18(minutes_1_out_7[11]), .out_19(minutes_1_out_7[12]), .out_20(minutes_1_out_7[13]),
    .S1_Comparer_Output(test_2_1_out_3[0]), .S2_Comparer_Output(test_2_1_out_3[1]));  // open: _24_hr_Clock_EN, Seconds_Set, Set_Alarm, Count_Down_Timer
  _7_Segment_Display u_7_segment_display_4 (
    .g(minutes_1_out_7[0]), .f(minutes_1_out_7[1]), .a(minutes_1_out_7[2]), .b(minutes_1_out_7[3]),
    .e(minutes_1_out_7[4]), .d(minutes_1_out_7[5]), .c(minutes_1_out_7[6]));  // open: dp
  _7_Segment_Display u_7_segment_display_5 (
    .g(seconds_1_out_7[0]), .f(seconds_1_out_7[1]), .a(seconds_1_out_7[2]), .b(seconds_1_out_7[3]),
    .e(seconds_1_out_7[4]), .d(seconds_1_out_7[5]), .c(seconds_1_out_7[6]));  // open: dp
  _7_Segment_Display u_7_segment_display_6 (
    .g(seconds_1_out_7[7]), .f(seconds_1_out_7[8]), .a(seconds_1_out_7[9]), .b(seconds_1_out_7[10]),
    .e(seconds_1_out_7[11]), .d(seconds_1_out_7[12]), .c(seconds_1_out_7[13]));  // open: dp
  Seconds seconds_1 (
    .RESET(in_3), ._12_hr_Clock_EN(RESET), .out_7(seconds_1_out_7[0]), .out_8(seconds_1_out_7[1]),
    .out_9(seconds_1_out_7[2]), .out_10(seconds_1_out_7[3]), .out_11(seconds_1_out_7[4]),
    .out_12(seconds_1_out_7[5]), .out_13(seconds_1_out_7[6]), .out_14(seconds_1_out_7[7]),
    .out_15(seconds_1_out_7[8]), .out_16(seconds_1_out_7[9]), .out_17(seconds_1_out_7[10]),
    .out_18(seconds_1_out_7[11]), .out_19(seconds_1_out_7[12]), .out_20(seconds_1_out_7[13]),
    .S1_Comparer_Output(minutes_1_out_7[0]), .S2_Comparer_Output(minutes_1_out_7[1]));  // open: _24_hr_Clock_EN, Seconds_Set, Set_Alarm, Count_Down_Timer
  AM_to_PM_LED am_to_pm_led_1 (
    .Reset(in_1), ._12hr_EN(RESET), .out_5(am_to_pm_led_1_out_5[0]), .out_6(am_to_pm_led_1_out_5[1]),
    .out_7(am_to_pm_led_1_out_5[2]), .out_8(am_to_pm_led_1_out_5[3]), .out_9(am_to_pm_led_1_out_5[4]),
    .out_10(am_to_pm_led_1_out_5[5]), .out_11(am_to_pm_led_1_out_5[6]));  // open: _24_hr_mode_turn_off, Toggler
  _7_Segment_Display u_7_segment_display_7 (
    .g(am_to_pm_led_1_out_5[0]), .f(am_to_pm_led_1_out_5[1]), .a(am_to_pm_led_1_out_5[2]),
    .b(am_to_pm_led_1_out_5[3]), .e(am_to_pm_led_1_out_5[4]), .d(am_to_pm_led_1_out_5[5]),
    .c(am_to_pm_led_1_out_5[6]));  // open: dp

  // Notes on the sheet:
  //   Hours
  //   HH
  //   Minutes
  //   MM
  //   Seconds
  //   SS
endmodule

module test_2 (
  input  EN,
  input  RESET,
  output out_3,
  output out_4,
  output out_5,
  output out_6,
  output out_7,
  output out_8,
  output out_9,
  output out_10,
  output out_11,
  output out_12,
  output out_13,
  output out_14,
  output out_15,
  output out_16,
  output out_17
);

  wire and_1_out, n12hourcounter_h1_1__12_hr_reset__1, n12hourcounter_h2_1__12_hr_reset__2;
  wire [1:0] n12hourcounter_h2_1_b1;
  wire [3:0] n12hourcounter_h1_1_q3;

  or or_1 (out_17, RESET, and_1_out);
  _12HourCounter_H1 u_12hourcounter_h1_1 (
    .EN(EN), .Reset(out_17), .Q3(n12hourcounter_h1_1_q3[0]), .Q2(n12hourcounter_h1_1_q3[1]),
    .Q1(n12hourcounter_h1_1_q3[2]), .Q0(n12hourcounter_h1_1_q3[3]),
    ._12_hr_Reset__1(n12hourcounter_h1_1__12_hr_reset__1));  // open: Overflow
  _12HourCounter_H2 u_12hourcounter_h2_1 (
    .EN(EN), .RESET(out_17), .B1(n12hourcounter_h2_1_b1[0]),
    ._12_hr_Reset__2(n12hourcounter_h2_1__12_hr_reset__2), .B0(n12hourcounter_h2_1_b1[1]));  // open: AM_PM_Overflow
  and and_1 (and_1_out, n12hourcounter_h2_1__12_hr_reset__2, n12hourcounter_h1_1__12_hr_reset__1);
  BCD_7_Segment_Display bcd_7_segment_display_1 (
    .A(n12hourcounter_h1_1_q3[0]), .B(n12hourcounter_h1_1_q3[1]), .C(n12hourcounter_h1_1_q3[2]),
    .D(n12hourcounter_h1_1_q3[3]), .a_2(out_3), .b_2(out_4), .c_2(out_5), .d_2(out_6), .e(out_7), .f(out_8),
    .g(out_9));
  BCD_7_Segment_Display bcd_7_segment_display_2 (
    .A(1'b0), .B(1'b0), .C(n12hourcounter_h2_1_b1[0]), .D(n12hourcounter_h2_1_b1[1]), .a_2(out_10),
    .b_2(out_11), .c_2(out_12), .d_2(out_13), .e(out_14), .f(out_15), .g(out_16));
endmodule

module S1_Alarm (
  input  EN,
  input  Reset,
  input  SecondToggle,
  output Q3,
  output Q2,
  output Overflow,
  output Q1,
  output Q0
);

  wire and_1_out, and_2_out, and_3_out, and_4_out, j_k_ff_1_qn;

  and and_1 (and_1_out, Q2, Q1, Q0);
  and and_2 (and_2_out, Q1, Q0);
  and and_3 (and_3_out, Q1, Q0);
  and and_4 (and_4_out, j_k_ff_1_qn, Q0);
  J_K_Flip_Flop j_k_ff_1 (
    .J(and_1_out), .clk(SecondToggle), .K(Q0), .Q(Q3), .Qn(j_k_ff_1_qn), .en(EN), .reset(Reset));  // open: preset
  J_K_Flip_Flop j_k_ff_2 (
    .J(and_2_out), .clk(SecondToggle), .K(and_3_out), .Q(Q2), .en(EN), .reset(Reset));  // open: Qn, preset
  J_K_Flip_Flop j_k_ff_3 (
    .J(and_4_out), .clk(SecondToggle), .K(Q0), .Q(Q1), .en(EN), .reset(Reset));  // open: Qn, preset
  J_K_Flip_Flop j_k_ff_4 (.J(1'b1), .clk(SecondToggle), .K(1'b1), .Q(Q0), .en(EN), .reset(Reset));  // open: Qn, preset
  nor nor_1 (Overflow, Q3, Q2, Q1, Q0);

  // Notes on the sheet:
  //   Q3
  //   Q2
  //   Q1
  //   Q0
endmodule

module S2_Alarm (
  input  EN,
  input  Reset,
  input  Second_Setter,
  output A2,
  output A1,
  output A0
);

  wire and_1_out, and_2_out, j_k_ff_1_qn, s1_alarm_1_overflow;

  S1_Alarm s1_alarm_1 (
    .EN(EN), .Reset(Reset), .SecondToggle(Second_Setter), .Overflow(s1_alarm_1_overflow));  // open: Q3, Q2, Q1, Q0
  and and_1 (and_1_out, A1, A0);
  and and_2 (and_2_out, j_k_ff_1_qn, A0);
  J_K_Flip_Flop j_k_ff_1 (
    .J(and_1_out), .clk(s1_alarm_1_overflow), .K(A0), .Q(A2), .Qn(j_k_ff_1_qn), .en(EN), .reset(Reset));  // open: preset
  J_K_Flip_Flop j_k_ff_2 (
    .J(and_2_out), .clk(s1_alarm_1_overflow), .K(A0), .Q(A1), .en(EN), .reset(Reset));  // open: Qn, preset
  J_K_Flip_Flop j_k_ff_3 (
    .J(1'b1), .clk(s1_alarm_1_overflow), .K(1'b1), .Q(A0), .en(EN), .reset(Reset));  // open: Qn, preset

  // Notes on the sheet:
  //   A2
  //   A1
  //   A0
endmodule

module M1_Alarm (
  input  EN,
  input  Reset,
  input  Minutes_Setter,
  output Q3,
  output Q2,
  output Overflow,
  output Q1,
  output Q0
);

  wire and_1_out, and_2_out, and_3_out, and_4_out, j_k_ff_1_qn;

  and and_1 (and_1_out, Q2, Q1, Q0);
  and and_2 (and_2_out, Q1, Q0);
  and and_3 (and_3_out, Q1, Q0);
  and and_4 (and_4_out, j_k_ff_1_qn, Q0);
  J_K_Flip_Flop j_k_ff_1 (
    .J(and_1_out), .clk(Minutes_Setter), .K(Q0), .Q(Q3), .Qn(j_k_ff_1_qn), .en(EN), .reset(Reset));  // open: preset
  J_K_Flip_Flop j_k_ff_2 (
    .J(and_2_out), .clk(Minutes_Setter), .K(and_3_out), .Q(Q2), .en(EN), .reset(Reset));  // open: Qn, preset
  J_K_Flip_Flop j_k_ff_3 (
    .J(and_4_out), .clk(Minutes_Setter), .K(Q0), .Q(Q1), .en(EN), .reset(Reset));  // open: Qn, preset
  J_K_Flip_Flop j_k_ff_4 (
    .J(1'b1), .clk(Minutes_Setter), .K(1'b1), .Q(Q0), .en(EN), .reset(Reset));  // open: Qn, preset
  nor nor_1 (Overflow, Q3, Q2, Q1, Q0);

  // Notes on the sheet:
  //   Q3
  //   Q2
  //   Q1
  //   Q0
endmodule

module M2_Alarm (
  input  EN,
  input  Reset,
  input  Minutes_Setter,
  output A2,
  output A1,
  output A0
);

  wire and_1_out, and_2_out, j_k_ff_1_qn, m1_alarm_1_overflow;

  M1_Alarm m1_alarm_1 (
    .EN(EN), .Reset(Reset), .Minutes_Setter(Minutes_Setter), .Overflow(m1_alarm_1_overflow));  // open: Q3, Q2, Q1, Q0
  and and_1 (and_1_out, A1, A0);
  and and_2 (and_2_out, j_k_ff_1_qn, A0);
  J_K_Flip_Flop j_k_ff_1 (
    .J(and_1_out), .clk(m1_alarm_1_overflow), .K(A0), .Q(A2), .Qn(j_k_ff_1_qn), .en(EN), .reset(Reset));  // open: preset
  J_K_Flip_Flop j_k_ff_2 (
    .J(and_2_out), .clk(m1_alarm_1_overflow), .K(A0), .Q(A1), .en(EN), .reset(Reset));  // open: Qn, preset
  J_K_Flip_Flop j_k_ff_3 (
    .J(1'b1), .clk(m1_alarm_1_overflow), .K(1'b1), .Q(A0), .en(EN), .reset(Reset));  // open: Qn, preset

  // Notes on the sheet:
  //   A2
  //   A1
  //   A0
endmodule

module H1_Alarm (
  input  EN,
  input  Reset,
  input  Hour_Setter,
  output Q3,
  output Q2,
  output Overflow,
  output Q1,
  output Q0,
  output _24_hr_Reset__1,
  output _12_hr_Reset_1
);

  wire and_1_out, and_2_out, and_3_out, and_4_out, j_k_ff_1_qn, j_k_ff_2_qn, j_k_ff_3_qn, j_k_ff_4_qn;

  and and_1 (and_1_out, Q2, Q1, Q0);
  and and_2 (and_2_out, Q1, Q0);
  and and_3 (and_3_out, Q1, Q0);
  and and_4 (and_4_out, j_k_ff_1_qn, Q0);
  J_K_Flip_Flop j_k_ff_1 (
    .J(and_1_out), .clk(Hour_Setter), .K(Q0), .Q(Q3), .Qn(j_k_ff_1_qn), .en(EN), .reset(Reset));  // open: preset
  J_K_Flip_Flop j_k_ff_2 (
    .J(and_2_out), .clk(Hour_Setter), .K(and_3_out), .Q(Q2), .Qn(j_k_ff_2_qn), .en(EN), .reset(Reset));  // open: preset
  J_K_Flip_Flop j_k_ff_3 (
    .J(and_4_out), .clk(Hour_Setter), .K(Q0), .Q(Q1), .Qn(j_k_ff_3_qn), .en(EN), .reset(Reset));  // open: preset
  J_K_Flip_Flop j_k_ff_4 (
    .J(1'b1), .clk(Hour_Setter), .K(1'b1), .Q(Q0), .Qn(j_k_ff_4_qn), .en(EN), .reset(Reset));  // open: preset
  nor nor_1 (Overflow, Q3, Q2, Q1, Q0);
  and and_5 (_24_hr_Reset__1, j_k_ff_1_qn, Q2, j_k_ff_3_qn, j_k_ff_4_qn);
  and and_6 (_12_hr_Reset_1, j_k_ff_1_qn, j_k_ff_2_qn, Q1, j_k_ff_4_qn);

  // Notes on the sheet:
  //   Q3
  //   Q2
  //   Q1
  //   Q0
endmodule

module H2_Alarm (
  input  EN,
  input  RESET,
  input  in_3,
  output B1,
  output _24_hr_Reset__2,
  output B0,
  output _12_hr_Reset__2
);

  wire h1_alarm_1_overflow, j_k_ff_1_qn;

  H1_Alarm h1_alarm_1 (
    .EN(EN), .Reset(RESET), .Hour_Setter(in_3), .Overflow(h1_alarm_1_overflow));  // open: Q3, Q2, Q1, Q0, _24_hr_Reset__1, _12_hr_Reset_1
  J_K_Flip_Flop j_k_ff_1 (
    .J(_12_hr_Reset__2), .clk(h1_alarm_1_overflow), .K(1'b1), .Q(_24_hr_Reset__2), .Qn(j_k_ff_1_qn), .en(EN),
    .reset(RESET));  // open: preset
  J_K_Flip_Flop j_k_ff_2 (
    .J(j_k_ff_1_qn), .clk(h1_alarm_1_overflow), .K(1'b1), .Q(_12_hr_Reset__2), .en(EN), .reset(RESET));  // open: Qn, preset

  assign B0 = _12_hr_Reset__2;
  assign B1 = _24_hr_Reset__2;

  // Notes on the sheet:
  //   B1
  //   B0
endmodule

module Multiplexer_Clock__Alarm_circuit (
  input  in_1,
  input  Clock,
  input  in_3,
  input  in_4,
  input  in_5,
  input  in_6,
  input  in_7,
  input  in_8,
  input  Set_Alarm_CountDownTimer,
  output out_10,
  output out_11,
  output out_12,
  output out_13
);

  Multiplexer #(.width(4), .enable("false")) multiplexer_1 (
    .in0({in_4, in_3, Clock, in_1}), .in1({in_8, in_7, in_6, in_5}), .out({out_13, out_12, out_11, out_10}),
    .sel(Set_Alarm_CountDownTimer));

  // Notes on the sheet:
  //   Alarm
endmodule

module Multiplexer_Compare (
  input  in_1,
  input  in_2,
  input  in_3,
  input  in_4,
  input  in_5,
  input  in_6,
  input  in_7,
  input  in_8,
  output out_9
);

  wire [3:0] not_1_out, xor_1_out;

  assign not_1_out = ~{in_8, in_7, in_6, in_5};  // NOT_Gate not_1, 4 bits wide
  assign xor_1_out = {in_4, in_3, in_2, in_1} ^ not_1_out;  // XOR_Gate xor_1, 4 bits wide
  and and_1 (out_9, xor_1_out[0], xor_1_out[1], xor_1_out[2], xor_1_out[3]);

  // Notes on the sheet:
  //   Clock
  //   Alarm
endmodule

module _30_second_Counter (
  input  Alarm_on_off,
  input  Input,
  input  Snooze,
  output LED_light_for_Alarm
);

  wire clock_1_out, nand_1_out, or_1_out, t_ff_1_q, t_ff_1_qn, t_ff_2_qn, t_ff_3_q, t_ff_3_qn, t_ff_4_q,
       t_ff_4_qn, t_ff_5_q;

  or or_1 (or_1_out, Input, Snooze);
  Clock clock_1 (.out(clock_1_out));
  T_Flip_Flop t_ff_1 (
    .clk(clock_1_out), .T(1'b1), .Q(t_ff_1_q), .Qn(t_ff_1_qn), .preset(Snooze), .reset(Input), .en(nand_1_out));
  T_Flip_Flop t_ff_2 (.clk(t_ff_1_qn), .T(1'b1), .Qn(t_ff_2_qn), .reset(or_1_out), .en(nand_1_out));  // open: Q, preset
  T_Flip_Flop t_ff_3 (
    .clk(t_ff_2_qn), .T(1'b1), .Q(t_ff_3_q), .Qn(t_ff_3_qn), .preset(Snooze), .reset(Input), .en(nand_1_out));
  T_Flip_Flop t_ff_4 (
    .clk(t_ff_3_qn), .T(1'b1), .Q(t_ff_4_q), .Qn(t_ff_4_qn), .preset(Snooze), .reset(Input), .en(nand_1_out));
  T_Flip_Flop t_ff_5 (
    .clk(t_ff_4_qn), .T(1'b1), .Q(t_ff_5_q), .preset(Snooze), .reset(Input), .en(nand_1_out));  // open: Qn
  and and_1 (LED_light_for_Alarm, t_ff_1_qn, Alarm_on_off);
  nand nand_1 (nand_1_out, t_ff_1_q, t_ff_2_qn, t_ff_3_q, t_ff_4_q, t_ff_5_q);
endmodule

module S1Countdown (
  input  EN,
  input  Reset,
  input  Second_setter,
  output Q3,
  output Q2,
  output Overflow,
  output Q1,
  output Q0
);

  wire and_1_out, and_2_out, and_3_out, and_4_out, and_5_out, clock_1_out, j_k_ff_2_qn, j_k_ff_3_qn,
       j_k_ff_4_qn, or_1_out, or_2_out;

  and and_1 (and_1_out, j_k_ff_2_qn, j_k_ff_3_qn, j_k_ff_4_qn);
  and and_2 (and_2_out, Q3, j_k_ff_4_qn);
  and and_3 (and_3_out, j_k_ff_3_qn, j_k_ff_4_qn);
  and and_4 (and_4_out, Q2, j_k_ff_4_qn);
  or or_1 (or_1_out, and_4_out, and_5_out);
  and and_5 (and_5_out, Q3, j_k_ff_4_qn);
  or or_2 (or_2_out, clock_1_out, Second_setter);
  Clock clock_1 (.out(clock_1_out));
  J_K_Flip_Flop j_k_ff_1 (
    .J(and_1_out), .clk(or_2_out), .K(j_k_ff_4_qn), .Q(Q3), .en(EN), .reset(Reset));  // open: Qn, preset
  J_K_Flip_Flop j_k_ff_2 (
    .J(and_2_out), .clk(or_2_out), .K(and_3_out), .Q(Q2), .Qn(j_k_ff_2_qn), .en(EN), .reset(Reset));  // open: preset
  J_K_Flip_Flop j_k_ff_3 (
    .J(or_1_out), .clk(or_2_out), .K(j_k_ff_4_qn), .Q(Q1), .Qn(j_k_ff_3_qn), .en(EN), .reset(Reset));  // open: preset
  J_K_Flip_Flop j_k_ff_4 (
    .J(1'b1), .clk(or_2_out), .K(1'b1), .Q(Q0), .Qn(j_k_ff_4_qn), .en(EN), .reset(Reset));  // open: preset
  and and_6 (Overflow, Q3, j_k_ff_2_qn, j_k_ff_3_qn, Q0);

  // Notes on the sheet:
  //   Clock
  //   Q3
  //   Q2
  //   Q1
  //   Q0
endmodule

module S2_Countdown (
  input  EN,
  input  Reset,
  input  Seconds_setter_enable,
  output A2,
  output Overflow,
  output A1,
  output A0
);

  wire and_1_out, and_2_out, j_k_ff_2_qn, j_k_ff_3_qn, s1countdown_1_overflow;

  S1Countdown s1countdown_1 (
    .EN(EN), .Reset(Reset), .Second_setter(Seconds_setter_enable), .Overflow(s1countdown_1_overflow));  // open: Q3, Q2, Q1, Q0
  and and_1 (and_1_out, j_k_ff_2_qn, j_k_ff_3_qn);
  and and_2 (and_2_out, A2, j_k_ff_3_qn);
  J_K_Flip_Flop j_k_ff_1 (
    .J(and_1_out), .clk(s1countdown_1_overflow), .K(j_k_ff_3_qn), .Q(A2), .en(EN), .reset(Reset));  // open: Qn, preset
  J_K_Flip_Flop j_k_ff_2 (
    .J(and_2_out), .clk(s1countdown_1_overflow), .K(j_k_ff_3_qn), .Q(A1), .Qn(j_k_ff_2_qn), .en(EN),
    .reset(Reset));  // open: preset
  J_K_Flip_Flop j_k_ff_3 (
    .J(1'b1), .clk(s1countdown_1_overflow), .K(1'b1), .Q(A0), .Qn(j_k_ff_3_qn), .en(EN), .reset(Reset));  // open: preset
  and and_3 (Overflow, A2, j_k_ff_2_qn, A0, Seconds_setter_enable);

  // Notes on the sheet:
  //   A2
  //   A1
  //   A0
endmodule

module M1_Countdown (
  input  EN,
  input  Reset,
  input  Minute_setter,
  output Q3,
  output Q2,
  output Overflow,
  output Q1,
  output Q0
);

  wire and_1_out, and_2_out, and_3_out, and_4_out, and_5_out, j_k_ff_2_qn, j_k_ff_3_qn, j_k_ff_4_qn,
       or_1_out, or_2_out, s2_countdown_1_overflow;

  S2_Countdown s2_countdown_1 (
    .EN(EN), .Reset(Reset), .Seconds_setter_enable(Minute_setter), .Overflow(s2_countdown_1_overflow));  // open: A2, A1, A0
  or or_1 (or_1_out, s2_countdown_1_overflow, Minute_setter);
  and and_1 (and_1_out, j_k_ff_2_qn, j_k_ff_3_qn, j_k_ff_4_qn);
  and and_2 (and_2_out, Q3, j_k_ff_4_qn);
  and and_3 (and_3_out, j_k_ff_3_qn, j_k_ff_4_qn);
  and and_4 (and_4_out, Q2, j_k_ff_4_qn);
  or or_2 (or_2_out, and_4_out, and_5_out);
  and and_5 (and_5_out, Q3, j_k_ff_4_qn);
  J_K_Flip_Flop j_k_ff_1 (
    .J(and_1_out), .clk(or_1_out), .K(j_k_ff_4_qn), .Q(Q3), .en(EN), .reset(Reset));  // open: Qn, preset
  J_K_Flip_Flop j_k_ff_2 (
    .J(and_2_out), .clk(or_1_out), .K(and_3_out), .Q(Q2), .Qn(j_k_ff_2_qn), .en(EN), .reset(Reset));  // open: preset
  J_K_Flip_Flop j_k_ff_3 (
    .J(or_2_out), .clk(or_1_out), .K(j_k_ff_4_qn), .Q(Q1), .Qn(j_k_ff_3_qn), .en(EN), .reset(Reset));  // open: preset
  J_K_Flip_Flop j_k_ff_4 (
    .J(1'b1), .clk(or_1_out), .K(1'b1), .Q(Q0), .Qn(j_k_ff_4_qn), .en(EN), .reset(Reset));  // open: preset
  and and_6 (Overflow, Q3, j_k_ff_2_qn, j_k_ff_3_qn, Q0);

  // Notes on the sheet:
  //   Q3
  //   Q2
  //   Q1
  //   Q0
endmodule

module M2_Countdown (
  input  EN,
  input  Reset,
  input  Minute_Setter,
  output A2,
  output Overflow,
  output A1,
  output A0
);

  wire and_1_out, and_2_out, j_k_ff_2_qn, j_k_ff_3_qn, m1_countdown_1_overflow;

  M1_Countdown m1_countdown_1 (
    .EN(EN), .Reset(Reset), .Minute_setter(Minute_Setter), .Overflow(m1_countdown_1_overflow));  // open: Q3, Q2, Q1, Q0
  and and_1 (and_1_out, j_k_ff_2_qn, j_k_ff_3_qn);
  and and_2 (and_2_out, A2, j_k_ff_3_qn);
  J_K_Flip_Flop j_k_ff_1 (
    .J(and_1_out), .clk(m1_countdown_1_overflow), .K(j_k_ff_3_qn), .Q(A2), .en(EN), .reset(Reset));  // open: Qn, preset
  J_K_Flip_Flop j_k_ff_2 (
    .J(and_2_out), .clk(m1_countdown_1_overflow), .K(j_k_ff_3_qn), .Q(A1), .Qn(j_k_ff_2_qn), .en(EN),
    .reset(Reset));  // open: preset
  J_K_Flip_Flop j_k_ff_3 (
    .J(1'b1), .clk(m1_countdown_1_overflow), .K(1'b1), .Q(A0), .Qn(j_k_ff_3_qn), .en(EN), .reset(Reset));  // open: preset
  and and_3 (Overflow, A2, j_k_ff_2_qn, A0, Minute_Setter);

  // Notes on the sheet:
  //   A2
  //   A1
  //   A0
endmodule

module H1_Countdown (
  input  EN,
  input  Reset,
  input  Hour_setter,
  output Q3,
  output Q2,
  output Overflow,
  output Q1,
  output Q0,
  output _24_hr_Reset__1,
  output _12_hr_Reset_1
);

  wire and_1_out, and_2_out, and_3_out, and_4_out, and_5_out, j_k_ff_1_qn, j_k_ff_2_qn, j_k_ff_3_qn,
       j_k_ff_4_qn, m2_countdown_1_overflow, or_1_out, or_2_out;

  M2_Countdown m2_countdown_1 (
    .EN(EN), .Reset(Reset), .Minute_Setter(Hour_setter), .Overflow(m2_countdown_1_overflow));  // open: A2, A1, A0
  or or_1 (or_1_out, m2_countdown_1_overflow, Hour_setter);
  and and_1 (and_1_out, j_k_ff_2_qn, j_k_ff_3_qn, j_k_ff_4_qn);
  and and_2 (and_2_out, Q3, j_k_ff_4_qn);
  and and_3 (and_3_out, j_k_ff_3_qn, j_k_ff_4_qn);
  and and_4 (and_4_out, Q2, j_k_ff_4_qn);
  or or_2 (or_2_out, and_4_out, and_5_out);
  and and_5 (and_5_out, Q3, j_k_ff_4_qn);
  J_K_Flip_Flop j_k_ff_1 (
    .J(and_1_out), .clk(or_1_out), .K(j_k_ff_4_qn), .Q(Q3), .Qn(j_k_ff_1_qn), .en(EN), .reset(Reset));  // open: preset
  J_K_Flip_Flop j_k_ff_2 (
    .J(and_2_out), .clk(or_1_out), .K(and_3_out), .Q(Q2), .Qn(j_k_ff_2_qn), .en(EN), .reset(Reset));  // open: preset
  J_K_Flip_Flop j_k_ff_3 (
    .J(or_2_out), .clk(or_1_out), .K(j_k_ff_4_qn), .Q(Q1), .Qn(j_k_ff_3_qn), .en(EN), .reset(Reset));  // open: preset
  J_K_Flip_Flop j_k_ff_4 (
    .J(1'b1), .clk(or_1_out), .K(1'b1), .Q(Q0), .Qn(j_k_ff_4_qn), .en(EN), .reset(Reset));  // open: preset
  and and_6 (Overflow, Q3, j_k_ff_2_qn, j_k_ff_3_qn, Q0);
  and and_7 (_24_hr_Reset__1, j_k_ff_1_qn, Q2, j_k_ff_3_qn, j_k_ff_4_qn);
  and and_8 (_12_hr_Reset_1, j_k_ff_1_qn, j_k_ff_2_qn, Q1, j_k_ff_4_qn);

  // Notes on the sheet:
  //   Q3
  //   Q2
  //   Q1
  //   Q0
endmodule

module H2_Countdown (
  input  EN,
  input  RESET,
  input  Hour_Setter,
  output B1,
  output _24_hr_Reset__2,
  output B0,
  output _12_hr_Reset__2
);

  wire h1_countdown_1_overflow, j_k_ff_2_qn;

  H1_Countdown h1_countdown_1 (
    .EN(EN), .Reset(RESET), .Hour_setter(Hour_Setter), .Overflow(h1_countdown_1_overflow));  // open: Q3, Q2, Q1, Q0, _24_hr_Reset__1, _12_hr_Reset_1
  J_K_Flip_Flop j_k_ff_1 (
    .J(j_k_ff_2_qn), .clk(h1_countdown_1_overflow), .K(1'b1), .Q(_24_hr_Reset__2), .en(EN), .reset(RESET));  // open: Qn, preset
  J_K_Flip_Flop j_k_ff_2 (
    .J(_24_hr_Reset__2), .clk(h1_countdown_1_overflow), .K(1'b1), .Q(_12_hr_Reset__2), .Qn(j_k_ff_2_qn),
    .en(EN), .reset(RESET));  // open: preset

  assign B0 = _12_hr_Reset__2;
  assign B1 = _24_hr_Reset__2;

  // Notes on the sheet:
  //   B1
  //   B0
endmodule
